// Logisim project drisc.circ as structural Verilog: 16 circuits, main circuit main
module main (
);

  wire address_selector_1_read_out, address_selector_1_write_out, address_selector_2_read_out,
       address_selector_3_write_out, address_selector_4_read_out, address_selector_5_read_out,
       address_selector_5_write_out, address_selector_6_read_out, address_selector_6_write_out, ALU_Use_PC,
       and_1_out, and_2_out, and_3_out, and_4_out, Cl0ck, comparator_1_eq, comparator_2_eq, comparator_3_eq,
       comparator_4_eq, csr_controller_1_system_load_out, Exception, Forward_Address, IO_Read, IO_Write,
       Jump, keyboard_1_avail, Load, Load_Upper_Immediate, Next_System_Load, or_1_out, Pad_Read, Pad_Write,
       PC_Read_Next, PC_Relative, Phase1, Phase2, Read_CSR, real_time_device_1_timer_interrupt,
       Register_File_Write, Reset, Software_Interrupt_Reg_q, Store, System_Jump, Use_Immediate;
  wire [1:0] Data_Offset, Pad_Data_Size;
  wire [2:0] Data_Type;
  wire [3:0] ALUComponent_cnzv, undriven_2, undriven_3;
  wire [4:0] OP_Function;
  wire [6:0] keyboard_1_data;
  wire [7:0] controlled_buffer_1_out, controlled_buffer_1_out_2, controlled_buffer_1_out_3,
       controlled_buffer_1_out_4, pla_1_out, pla_2_out, pla_3_out, pla_4_out;
  wire [7:7] not_1_out;
  wire [9:0] OperationController_next_decoded_instruction;
  wire [14:0] Register_Addresses;
  wire [15:0] random_1_out;
  wire [31:0] address_selector_1_address_out, address_selector_3_address_out, address_selector_4_address_out,
       address_selector_5_address_out, address_selector_6_address_out, ALUComponent_result,
       csr_controller_1_c_bus, csr_controller_1_system_target_address, DataIO_cpu_out, multiplexer_1_out,
       multiplexer_2_out, multiplexer_3_out, multiplexer_4_out, OperationController_current_instruction_out,
       OperationController_immediate_out, OperationController_next_instruction_out,
       ProgramCounter_address_bus_out, ProgramCounter_calculated_address, ProgramCounter_current_out,
       ProgramCounter_next_out, real_time_device_1_data_out, register_1_q, RegisterFile_a_bus_out,
       RegisterFile_b_bus_out, undriven;

  // Probe on Register_Addresses[4:0]
  // Probe on Register_Addresses[9:5]
  // Probe on Register_Addresses[14:10]
  Register_File RegisterFile (
    .C_Bus_In(multiplexer_1_out), .Addresses_In(Register_Addresses), .Write(Register_File_Write),
    .Clock(Cl0ck), .Reset(Reset), .A_Bus_Out(RegisterFile_a_bus_out), .B_Bus_Out(RegisterFile_b_bus_out));
  // Probe on RegisterFile_a_bus_out
  // Probe on RegisterFile_b_bus_out
  // Probe on multiplexer_1_out
  assign {controlled_buffer_1_out_4, controlled_buffer_1_out_3, controlled_buffer_1_out_2, controlled_buffer_1_out} = Pad_Write ? RegisterFile_b_bus_out : 32'bz;  // Controlled_Buffer controlled_buffer_1
  Multiplexer #(.width(32)) multiplexer_1 (
    .in0(multiplexer_2_out), .in1(DataIO_cpu_out), .out(multiplexer_1_out), .sel(IO_Read));
  Input_Buffer DataIO (
    .IO_In({controlled_buffer_1_out_4, controlled_buffer_1_out_3, controlled_buffer_1_out_2, controlled_buffer_1_out}),
    .Write(IO_Write), .Clock(Cl0ck), .Data_Offset(Data_Offset), .Data_Type(Data_Type),
    .CPU_Out(DataIO_cpu_out));
  Multiplexer #(.width(32)) multiplexer_2 (
    .in0(multiplexer_3_out), .in1(OperationController_immediate_out), .out(multiplexer_2_out),
    .sel(Load_Upper_Immediate));
  T_Flip_Flop t_ff_1 (.clk(Cl0ck), .T(1'b1), .Q(Phase2), .Qn(Phase1), .reset(Reset));  // open: preset
  Multiplexer #(.width(32)) multiplexer_3 (
    .in0(multiplexer_4_out), .in1(ProgramCounter_next_out), .out(multiplexer_3_out), .sel(PC_Read_Next));
  Multiplexer #(.width(32)) multiplexer_4 (
    .in0(ALUComponent_result), .in1(csr_controller_1_c_bus), .out(multiplexer_4_out), .sel(Read_CSR));
  ALU ALUComponent (
    .Operation(OP_Function), .Use_PC(ALU_Use_PC), .Use_Immediate(Use_Immediate), .a(RegisterFile_a_bus_out),
    .Program_Counter_In(ProgramCounter_current_out), .b(RegisterFile_b_bus_out),
    .Immediate(OperationController_immediate_out), .Result(ALUComponent_result), .CNZV(ALUComponent_cnzv));
  Operation_Controller OperationController (
    .Next_System_Load(Next_System_Load),
    .Data_In({controlled_buffer_1_out_4, controlled_buffer_1_out_3, controlled_buffer_1_out_2, controlled_buffer_1_out}),
    .Clock(Cl0ck), .Reset(Reset), .Exception(Exception), .Phase1(Phase1), .Phase2(Phase2),
    .CNZV(ALUComponent_cnzv), .System_Jump(System_Jump), .Data_Type_Out(Data_Type),
    .Register_Addresses(Register_Addresses), .Immediate_Out(OperationController_immediate_out),
    .Store_Out(Store), .Load_Out(Load), .PC_Forward_Address(Forward_Address),
    .Load_Upper_Immediate(Load_Upper_Immediate), .PC_Relative(PC_Relative),
    .Register_File_Write(Register_File_Write), .PC_Read_Next(PC_Read_Next), .Jump(Jump),
    .ALU_Use_PC(ALU_Use_PC), .ALU_Use_Immediate(Use_Immediate), .ALU_OP_Function(OP_Function),
    .Input_Buffer_Read(IO_Read), .PAD_Write(Pad_Write), .Input_Buffer_Write(IO_Write),
    .PAD_Data_Size(Pad_Data_Size), .PAD_Read(Pad_Read),
    .Next_Instruction_Out(OperationController_next_instruction_out),
    .Current_Instruction_Out(OperationController_current_instruction_out),
    .Next_Decoded_Instruction(OperationController_next_decoded_instruction));
  // Probe on ProgramCounter_current_out
  // Probe on OperationController_immediate_out
  CSR_Controller csr_controller_1 (
    .Reset(Reset), .Clock(Cl0ck), .A_Bus(RegisterFile_a_bus_out), .Current_PC(ProgramCounter_current_out),
    .Pad_Software_Interrupt(Software_Interrupt_Reg_q),
    .Pad_Timer_Interrupt(real_time_device_1_timer_interrupt), .Pad_External_Interrupt(keyboard_1_avail),
    .Store(Store), .Jump(Jump), .Load(Load),
    .Next_Decoded_Instruction(OperationController_next_decoded_instruction),
    .Calculated_Address(ProgramCounter_calculated_address),
    .Current_Instruction(OperationController_current_instruction_out),
    .Next_Instruction(OperationController_next_instruction_out), .Phase1(Phase1), .Phase2(Phase2),
    .Read_CSR(Read_CSR), .System_Target_Address(csr_controller_1_system_target_address),
    .Next_System_Load(Next_System_Load), .System_Load_Out(csr_controller_1_system_load_out),
    .System_Jump(System_Jump), .C_Bus(csr_controller_1_c_bus), .Exception(Exception));
  Program_Counter ProgramCounter (
    .Forward_Address(Forward_Address), .PC_Relative(PC_Relative), .Address_In(RegisterFile_a_bus_out),
    .Immediate(OperationController_immediate_out),
    .System_Target_Address(csr_controller_1_system_target_address), .Jump(Jump), .System_Jump(System_Jump),
    .Write(Phase2), .Reset(Reset), .Clock(Cl0ck), .Use_Offset(Store),
    .System_Load(csr_controller_1_system_load_out), .Address_Bus_Out(ProgramCounter_address_bus_out),
    .Byte_Offset(Data_Offset), .Current_Out(ProgramCounter_current_out), .Next_Out(ProgramCounter_next_out),
    .Calculated_Address(ProgramCounter_calculated_address));
  // Probe on {controlled_buffer_1_out_4, controlled_buffer_1_out_3, controlled_buffer_1_out_2, controlled_buffer_1_out}
  // Probe on ProgramCounter_address_bus_out
  Clock MainClock (.out(Cl0ck));
  POR #(.PorHighDuration(1), .porsize(2)) por_1 (.out(Reset));
  Address_Selector address_selector_1 (
    .Read_In(Pad_Read), .Write_In(Pad_Write), .Address_In(ProgramCounter_address_bus_out),
    .Min_Address({32{1'b0}}), .Max_Address(32'hfffffc), .Read_Out(address_selector_1_read_out),
    .Write_Out(address_selector_1_write_out), .Address_Out(address_selector_1_address_out));
  Address_Selector address_selector_2 (
    .Read_In(Pad_Read), .Address_In(ProgramCounter_address_bus_out), .Min_Address(32'hfffffc),
    .Max_Address(32'h1000000), .Read_Out(address_selector_2_read_out));  // open: Write_In, Write_Out, Address_Out
  Address_Selector address_selector_3 (
    .Write_In(Pad_Write), .Address_In(ProgramCounter_address_bus_out), .Min_Address(32'h1000000),
    .Max_Address(32'h1100000), .Write_Out(address_selector_3_write_out),
    .Address_Out(address_selector_3_address_out));  // open: Read_In, Read_Out
  Comparator #(.width(32)) comparator_1 (
    .a(ProgramCounter_address_bus_out), .b(32'h1100000), .eq(comparator_1_eq));  // open: gt, lt
  Comparator #(.width(32)) comparator_2 (
    .a(ProgramCounter_address_bus_out), .b(32'h1100001), .eq(comparator_2_eq));  // open: gt, lt
  Comparator #(.width(32)) comparator_3 (
    .a(ProgramCounter_address_bus_out), .b(32'h1100010), .eq(comparator_3_eq));  // open: gt, lt
  assign {controlled_buffer_1_out_4, controlled_buffer_1_out_3, controlled_buffer_1_out_2, controlled_buffer_1_out} = address_selector_4_read_out ? undriven : 32'bz;  // Controlled_Buffer controlled_buffer_2
  Address_Selector address_selector_4 (
    .Read_In(Pad_Read), .Write_In(Pad_Write), .Address_In(ProgramCounter_address_bus_out),
    .Min_Address(32'h80000000), .Max_Address(32'h81000000), .Read_Out(address_selector_4_read_out),
    .Address_Out(address_selector_4_address_out));  // open: Write_Out
  Address_Selector address_selector_5 (
    .Read_In(Pad_Read), .Write_In(Pad_Write), .Address_In(ProgramCounter_address_bus_out),
    .Min_Address(32'h81000000), .Max_Address(32'h81000010), .Read_Out(address_selector_5_read_out),
    .Write_Out(address_selector_5_write_out), .Address_Out(address_selector_5_address_out));
  Comparator #(.width(32)) comparator_4 (
    .a(ProgramCounter_address_bus_out), .b(32'h81000010), .eq(comparator_4_eq));  // open: gt, lt
  Address_Selector address_selector_6 (
    .Read_In(Pad_Read), .Write_In(Pad_Write), .Address_In(ProgramCounter_address_bus_out),
    .Min_Address(32'hff000000), .Max_Address({32{1'b1}}), .Read_Out(address_selector_6_read_out),
    .Write_Out(address_selector_6_write_out), .Address_Out(address_selector_6_address_out));
  // RAM #(.addrWidth(24), .databus("bidir"), .enables("line"), .line("quad"), .misaligned("true"), .\type ("nonvolatile")) ram_1: pin names not known; wires that end beside it: address_selector_1_address_out[23:0], address_selector_1_write_out, address_selector_1_read_out, 1'b1, Pad_Data_Size[1], Cl0ck
  Keyboard keyboard_1 (
    .clk(Cl0ck), .re(address_selector_2_read_out), .avail(keyboard_1_avail), .data(keyboard_1_data));  // open: clr
  and and_1 (and_1_out, comparator_1_eq, Pad_Write);
  and and_2 (and_2_out, Pad_Write, comparator_2_eq);
  Register #(.width(32)) register_1 (
    .D({controlled_buffer_1_out_4, controlled_buffer_1_out_3, controlled_buffer_1_out_2, controlled_buffer_1_out}),
    .en(and_3_out), .clk(Cl0ck), .Q(register_1_q), .clr(Reset));
  and and_3 (and_3_out, Pad_Write, comparator_3_eq);
  // ROM #(.addrWidth(16), .line("quad")) Trap_Handler: pin names not known
  assign {controlled_buffer_1_out_4, controlled_buffer_1_out_3, controlled_buffer_1_out_2, controlled_buffer_1_out} = address_selector_5_read_out ? real_time_device_1_data_out : 32'bz;  // Controlled_Buffer controlled_buffer_3
  Register #(.width(1)) Software_Interrupt_Reg (
    .D(controlled_buffer_1_out[0]), .en(and_4_out), .clk(Cl0ck), .Q(Software_Interrupt_Reg_q), .clr(Reset));
  and and_4 (and_4_out, Pad_Write, comparator_4_eq);
  // RAM #(.addrWidth(24), .databus("bidir"), .enables("line"), .line("quad")) OS_RAM: pin names not known; wires that end beside it: address_selector_6_address_out[23:0], address_selector_6_write_out, address_selector_6_read_out, 1'b1, Pad_Data_Size[1], Cl0ck
  PLA #(.in_width(8), .out_width(8), .\table ("00000000 00000000 # NULL\n00000001 00000000 # SOH\n00000010 00000000 # STX\n00000011 00000000 # ETX\n00000100 00000000 # EOT\n00000101 00000000 # ENQ\n00000110 00000000 # ACK\n00000111 00000000 # BEL\n00001000 00000000 # BS\n00001001 00000000 # TAB\n00001010 00000000 # LF\n00001011 00000000 # VT\n00001100 00000000 # FF\n00001101 00000000 # CR\n00001110 00000000 # SO\n00001111 00000000 # SI\n00010000 00000000 # DLE\n00010001 00000000 # DC1\n00010010 00000000 # DC2\n00010011 00000000 # DC3\n00010100 00000000 # DC4\n00010101 00000000 # NAK\n00010110 00000000 # SYN\n00010111 00000000 # ETB\n00011000 00000000 # CAN\n00011001 00000000 # EM\n00011010 00000000 # SUB\n00011011 00000000 # ESC\n00011100 00000000 # FS\n00011101 00000000 # GS\n00011110 00000000 # RS\n00011111 00000000 # US\n00100000 00000000 # Space\n00100001 10000110 # !\n00100010 00100010 # \"\n00100011 01100110 # #\n00100100 01101101 # $\n00100101 01001001 # %\n00100110 01111111 # &\n00100111 00000010 # '\n00101000 00111001 # (\n00101001 00001111 # )\n00101010 01100011 # *\n00101011 01000000 # +\n00101100 10000000 # ,\n00101101 01000000 # -\n00101110 10000000 # .\n00101111 01010010 # /\n00110000 00111111 # 0\n00110001 00000110 # 1\n00110010 01011011 # 2\n00110011 01001111 # 3\n00110100 01100110 # 4\n00110101 01101101 # 5\n00110100 01100110 # 4\n00110101 01101101 # 5\n00110110 01111101 # 6\n00110111 00000111 # 7\n00111000 01111111 # 8\n00111001 01101111 # 9\n00111010 10000010 # :\n00111011 10000010 # ;\n00111100 01100000 # <\n00111101 01001000 # =\n00111110 01000010 # >\n00111111 11010011 # ?\n01000000 01011111 # @\n01000001 01110111 # A\n01000010 01111111 # B\n01000011 00111001 # C\n01000100 01011110 # D\n01000101 01111001 # E\n01000110 01110001 # F\n01000111 00111101 # G\n01001000 01110110 # H\n01001001 00000110 # I\n01001010 00011110 # J\n01001011 01110110 # K\n01001100 00111000 # L\n01001101 00010101 # M\n01001110 01010100 # N\n01001111 00111111 # O\n01010000 01110011 # P\n01010001 01100111 # Q\n01010010 01010000 # R\n01010011 01101101 # S\n01010100 01111000 # T\n01010101 00111110 # U\n01010110 00011100 # V\n01010111 00101010 # W\n01011000 01110110 # X\n01011001 01101110 # Y\n01011010 01011011 # Z\n01011011 00111001 # [\n01011100 00110001 # \\\n01011101 00001111 # ]\n01011110 01100011 # ^\n01011111 00001000 # _\n01100000 00000010 # `\n01100001 01110111 # a\n01100010 01111100 # b\n01100011 01011000 # c\n01100100 01011110 # d\n01100101 01111001 # e\n01100110 01110001 # f\n01100111 01101111 # g\n01101000 01110100 # h\n01101001 00000100 # i\n01101010 00001110 # j\n01101011 01110110 # k\n01101100 00110000 # l\n01101101 00010100 # m\n01101110 01010100 # n\n01101111 01011100 # o\n01110000 01110011 # p\n01110001 01100111 # q\n01110010 01010000 # r\n01110011 01101101 # s\n01110100 01111000 # t\n01110101 00011100 # u\n01110110 00011100 # v\n01110111 00101010 # w\n01111000 01110110 # x\n01111001 01101110 # y\n01111010 01011011 # z\n01111011 00111001 # {\n01111100 00000110 # |\n01111101 00001111 # }\n01111110 01000000 # ~\n01111111 00000000 # DEL\n10000000 11000000 # Ç\n10000001 11111001 # ü\n10000010 10100100 # é\n10000011 10110000 # â\n10000100 10011001 # ä\n10000101 10001010 # à\n10000100 10011001 # ä\n10000101 10001010 # à\n10000110 10000110 # å\n10000111 11001110 # ç\n10001000 10100000 # ê\n10001001 10010010 # ë\n10001010 10001000 # è\n10001011 10010100 # ï\n10001100 11000110 # î\n10001101 11010000 # ì\n10001110 10101011 # Ä\n10001111 10011100 # Å\n10010000 10001110 # É\n10010001 11111000 # æ\n10010010 11111101 # Æ\n10010011 10011100 # ô\n10010100 10010000 # ö\n10010101 11000000 # ò\n10010110 11110000 # û\n10010111 11000000 # ù\n10011000 10001001 # ÿ\n10011001 01101110 # Ö\n10011010 01111001 # Ü\n10011011 11000110 # ¢\n10011100 10100011 # £\n10011101 10010001 # ¥\n10011110 01011100 # ₧\n10011111 01110011 # ƒ\n10100000 00000000 #  \n10100001 10000110 # ¡\n10100010 01011110 # ¢\n10100011 10100011 # £\n10100100 10010001 # ¤\n10100101 10010001 # ¥\n10100110 00000110 # ¦\n10100111 01001111 # §\n10101000 00100010 # ¨\n10101001 01110111 # ©\n10101010 00011110 # ª\n10101011 01100000 # «\n10101100 01000000 # ¬\n10101101 10000000 # ­\n10101110 01110111 # ®\n10101111 01000000 # ¯\n10110000 01100011 # °\n10110001 01000000 # ±\n10110010 01011011 # ²\n10110011 01001111 # ³\n10110100 00000010 # ´\n10110101 01111100 # µ\n10110110 01011110 # ¶\n10110111 10000000 # ·\n10111000 00000010 # ¸\n10111001 00000110 # ¹\n10111010 00011110 # º\n10111011 01000010 # »\n10111100 01100110 # ¼\n10111101 01101101 # ½\n10111110 01111101 # ¾\n10111111 11010011 # ¿\n11000000 01110111 # À\n11000001 01110111 # Á\n11000010 01110111 # Â\n11000011 01110111 # Ã\n11000100 01110111 # Ä\n11000101 01110111 # Å\n11000110 11111101 # Æ\n11000111 00111001 # Ç\n11001000 01111001 # È\n11001001 01111001 # É\n11001010 01111001 # Ê\n11001011 01111001 # Ë\n11001100 00000110 # Ì\n11001101 00000110 # Í\n11001110 00000110 # Î\n11001111 00000110 # Ï\n11010000 01111110 # Ð\n11010001 01010100 # Ñ\n11010010 00111111 # Ò\n11010011 00111111 # Ó\n11010100 00111111 # Ô\n11010101 00111111 # Õ\n11010110 00111111 # Ö\n11010111 01000000 # ×\n11011000 00111111 # Ø\n11011001 00111110 # Ù\n11011010 00111110 # Ú\n11011011 00111110 # Û\n11011100 00111110 # Ü\n11011101 01101110 # Ý\n11011110 01110010 # Þ\n11011111 01111101 # ß\n11100000 01110111 # à\n11100001 01110111 # á\n11100010 01110111 # â\n11100011 01110111 # ã\n11100100 01110111 # ä\n11100100 01110111 # ä\n11100101 01110111 # å\n11100110 11111001 # æ\n11100111 01011000 # ç\n11101000 01111001 # è\n11101001 01111001 # é\n11101010 01111001 # ê\n11101011 01111001 # ë\n11101100 00000100 # ì\n11101101 00000100 # í\n11101110 00000100 # î\n11101111 00000100 # ï\n11110000 01111101 # ð\n11110001 01010100 # ñ\n11110010 01011100 # ò\n11110011 01011100 # ó\n11110100 01011100 # ô\n11110101 01011100 # õ\n11110110 01011100 # ö\n11110111 01000000 # ÷\n11111000 01011100 # ø\n11111001 00011100 # ù\n11111010 00011100 # ú\n11111011 00011100 # û\n11111100 00011100 # ü\n11111101 01101110 # ý\n11111110 01110010 # þ\n11111111 00011100 # ÿ")) pla_1 (
    .in(register_1_q[7:0]), .out(pla_1_out));
  PLA #(.in_width(8), .out_width(8), .\table ("00000000 00000000 # NULL\n00000001 00000000 # SOH\n00000010 00000000 # STX\n00000011 00000000 # ETX\n00000100 00000000 # EOT\n00000101 00000000 # ENQ\n00000110 00000000 # ACK\n00000111 00000000 # BEL\n00001000 00000000 # BS\n00001001 00000000 # TAB\n00001010 00000000 # LF\n00001011 00000000 # VT\n00001100 00000000 # FF\n00001101 00000000 # CR\n00001110 00000000 # SO\n00001111 00000000 # SI\n00010000 00000000 # DLE\n00010001 00000000 # DC1\n00010010 00000000 # DC2\n00010011 00000000 # DC3\n00010100 00000000 # DC4\n00010101 00000000 # NAK\n00010110 00000000 # SYN\n00010111 00000000 # ETB\n00011000 00000000 # CAN\n00011001 00000000 # EM\n00011010 00000000 # SUB\n00011011 00000000 # ESC\n00011100 00000000 # FS\n00011101 00000000 # GS\n00011110 00000000 # RS\n00011111 00000000 # US\n00100000 00000000 # Space\n00100001 10000110 # !\n00100010 00100010 # \"\n00100011 01100110 # #\n00100100 01101101 # $\n00100101 01001001 # %\n00100110 01111111 # &\n00100111 00000010 # '\n00101000 00111001 # (\n00101001 00001111 # )\n00101010 01100011 # *\n00101011 01000000 # +\n00101100 10000000 # ,\n00101101 01000000 # -\n00101110 10000000 # .\n00101111 01010010 # /\n00110000 00111111 # 0\n00110001 00000110 # 1\n00110010 01011011 # 2\n00110011 01001111 # 3\n00110100 01100110 # 4\n00110101 01101101 # 5\n00110100 01100110 # 4\n00110101 01101101 # 5\n00110110 01111101 # 6\n00110111 00000111 # 7\n00111000 01111111 # 8\n00111001 01101111 # 9\n00111010 10000010 # :\n00111011 10000010 # ;\n00111100 01100000 # <\n00111101 01001000 # =\n00111110 01000010 # >\n00111111 11010011 # ?\n01000000 01011111 # @\n01000001 01110111 # A\n01000010 01111111 # B\n01000011 00111001 # C\n01000100 01011110 # D\n01000101 01111001 # E\n01000110 01110001 # F\n01000111 00111101 # G\n01001000 01110110 # H\n01001001 00000110 # I\n01001010 00011110 # J\n01001011 01110110 # K\n01001100 00111000 # L\n01001101 00010101 # M\n01001110 01010100 # N\n01001111 00111111 # O\n01010000 01110011 # P\n01010001 01100111 # Q\n01010010 01010000 # R\n01010011 01101101 # S\n01010100 01111000 # T\n01010101 00111110 # U\n01010110 00011100 # V\n01010111 00101010 # W\n01011000 01110110 # X\n01011001 01101110 # Y\n01011010 01011011 # Z\n01011011 00111001 # [\n01011100 00110001 # \\\n01011101 00001111 # ]\n01011110 01100011 # ^\n01011111 00001000 # _\n01100000 00000010 # `\n01100001 01110111 # a\n01100010 01111100 # b\n01100011 01011000 # c\n01100100 01011110 # d\n01100101 01111001 # e\n01100110 01110001 # f\n01100111 01101111 # g\n01101000 01110100 # h\n01101001 00000100 # i\n01101010 00001110 # j\n01101011 01110110 # k\n01101100 00110000 # l\n01101101 00010100 # m\n01101110 01010100 # n\n01101111 01011100 # o\n01110000 01110011 # p\n01110001 01100111 # q\n01110010 01010000 # r\n01110011 01101101 # s\n01110100 01111000 # t\n01110101 00011100 # u\n01110110 00011100 # v\n01110111 00101010 # w\n01111000 01110110 # x\n01111001 01101110 # y\n01111010 01011011 # z\n01111011 00111001 # {\n01111100 00000110 # |\n01111101 00001111 # }\n01111110 01000000 # ~\n01111111 00000000 # DEL\n10000000 11000000 # Ç\n10000001 11111001 # ü\n10000010 10100100 # é\n10000011 10110000 # â\n10000100 10011001 # ä\n10000101 10001010 # à\n10000100 10011001 # ä\n10000101 10001010 # à\n10000110 10000110 # å\n10000111 11001110 # ç\n10001000 10100000 # ê\n10001001 10010010 # ë\n10001010 10001000 # è\n10001011 10010100 # ï\n10001100 11000110 # î\n10001101 11010000 # ì\n10001110 10101011 # Ä\n10001111 10011100 # Å\n10010000 10001110 # É\n10010001 11111000 # æ\n10010010 11111101 # Æ\n10010011 10011100 # ô\n10010100 10010000 # ö\n10010101 11000000 # ò\n10010110 11110000 # û\n10010111 11000000 # ù\n10011000 10001001 # ÿ\n10011001 01101110 # Ö\n10011010 01111001 # Ü\n10011011 11000110 # ¢\n10011100 10100011 # £\n10011101 10010001 # ¥\n10011110 01011100 # ₧\n10011111 01110011 # ƒ\n10100000 00000000 #  \n10100001 10000110 # ¡\n10100010 01011110 # ¢\n10100011 10100011 # £\n10100100 10010001 # ¤\n10100101 10010001 # ¥\n10100110 00000110 # ¦\n10100111 01001111 # §\n10101000 00100010 # ¨\n10101001 01110111 # ©\n10101010 00011110 # ª\n10101011 01100000 # «\n10101100 01000000 # ¬\n10101101 10000000 # ­\n10101110 01110111 # ®\n10101111 01000000 # ¯\n10110000 01100011 # °\n10110001 01000000 # ±\n10110010 01011011 # ²\n10110011 01001111 # ³\n10110100 00000010 # ´\n10110101 01111100 # µ\n10110110 01011110 # ¶\n10110111 10000000 # ·\n10111000 00000010 # ¸\n10111001 00000110 # ¹\n10111010 00011110 # º\n10111011 01000010 # »\n10111100 01100110 # ¼\n10111101 01101101 # ½\n10111110 01111101 # ¾\n10111111 11010011 # ¿\n11000000 01110111 # À\n11000001 01110111 # Á\n11000010 01110111 # Â\n11000011 01110111 # Ã\n11000100 01110111 # Ä\n11000101 01110111 # Å\n11000110 11111101 # Æ\n11000111 00111001 # Ç\n11001000 01111001 # È\n11001001 01111001 # É\n11001010 01111001 # Ê\n11001011 01111001 # Ë\n11001100 00000110 # Ì\n11001101 00000110 # Í\n11001110 00000110 # Î\n11001111 00000110 # Ï\n11010000 01111110 # Ð\n11010001 01010100 # Ñ\n11010010 00111111 # Ò\n11010011 00111111 # Ó\n11010100 00111111 # Ô\n11010101 00111111 # Õ\n11010110 00111111 # Ö\n11010111 01000000 # ×\n11011000 00111111 # Ø\n11011001 00111110 # Ù\n11011010 00111110 # Ú\n11011011 00111110 # Û\n11011100 00111110 # Ü\n11011101 01101110 # Ý\n11011110 01110010 # Þ\n11011111 01111101 # ß\n11100000 01110111 # à\n11100001 01110111 # á\n11100010 01110111 # â\n11100011 01110111 # ã\n11100100 01110111 # ä\n11100100 01110111 # ä\n11100101 01110111 # å\n11100110 11111001 # æ\n11100111 01011000 # ç\n11101000 01111001 # è\n11101001 01111001 # é\n11101010 01111001 # ê\n11101011 01111001 # ë\n11101100 00000100 # ì\n11101101 00000100 # í\n11101110 00000100 # î\n11101111 00000100 # ï\n11110000 01111101 # ð\n11110001 01010100 # ñ\n11110010 01011100 # ò\n11110011 01011100 # ó\n11110100 01011100 # ô\n11110101 01011100 # õ\n11110110 01011100 # ö\n11110111 01000000 # ÷\n11111000 01011100 # ø\n11111001 00011100 # ù\n11111010 00011100 # ú\n11111011 00011100 # û\n11111100 00011100 # ü\n11111101 01101110 # ý\n11111110 01110010 # þ\n11111111 00011100 # ÿ")) pla_2 (
    .in(register_1_q[23:16]), .out(pla_2_out));
  not not_1 (not_1_out[7], keyboard_1_avail);
  PLA #(.in_width(8), .out_width(8), .\table ("00000000 00000000 # NULL\n00000001 00000000 # SOH\n00000010 00000000 # STX\n00000011 00000000 # ETX\n00000100 00000000 # EOT\n00000101 00000000 # ENQ\n00000110 00000000 # ACK\n00000111 00000000 # BEL\n00001000 00000000 # BS\n00001001 00000000 # TAB\n00001010 00000000 # LF\n00001011 00000000 # VT\n00001100 00000000 # FF\n00001101 00000000 # CR\n00001110 00000000 # SO\n00001111 00000000 # SI\n00010000 00000000 # DLE\n00010001 00000000 # DC1\n00010010 00000000 # DC2\n00010011 00000000 # DC3\n00010100 00000000 # DC4\n00010101 00000000 # NAK\n00010110 00000000 # SYN\n00010111 00000000 # ETB\n00011000 00000000 # CAN\n00011001 00000000 # EM\n00011010 00000000 # SUB\n00011011 00000000 # ESC\n00011100 00000000 # FS\n00011101 00000000 # GS\n00011110 00000000 # RS\n00011111 00000000 # US\n00100000 00000000 # Space\n00100001 10000110 # !\n00100010 00100010 # \"\n00100011 01100110 # #\n00100100 01101101 # $\n00100101 01001001 # %\n00100110 01111111 # &\n00100111 00000010 # '\n00101000 00111001 # (\n00101001 00001111 # )\n00101010 01100011 # *\n00101011 01000000 # +\n00101100 10000000 # ,\n00101101 01000000 # -\n00101110 10000000 # .\n00101111 01010010 # /\n00110000 00111111 # 0\n00110001 00000110 # 1\n00110010 01011011 # 2\n00110011 01001111 # 3\n00110100 01100110 # 4\n00110101 01101101 # 5\n00110100 01100110 # 4\n00110101 01101101 # 5\n00110110 01111101 # 6\n00110111 00000111 # 7\n00111000 01111111 # 8\n00111001 01101111 # 9\n00111010 10000010 # :\n00111011 10000010 # ;\n00111100 01100000 # <\n00111101 01001000 # =\n00111110 01000010 # >\n00111111 11010011 # ?\n01000000 01011111 # @\n01000001 01110111 # A\n01000010 01111111 # B\n01000011 00111001 # C\n01000100 01011110 # D\n01000101 01111001 # E\n01000110 01110001 # F\n01000111 00111101 # G\n01001000 01110110 # H\n01001001 00000110 # I\n01001010 00011110 # J\n01001011 01110110 # K\n01001100 00111000 # L\n01001101 00010101 # M\n01001110 01010100 # N\n01001111 00111111 # O\n01010000 01110011 # P\n01010001 01100111 # Q\n01010010 01010000 # R\n01010011 01101101 # S\n01010100 01111000 # T\n01010101 00111110 # U\n01010110 00011100 # V\n01010111 00101010 # W\n01011000 01110110 # X\n01011001 01101110 # Y\n01011010 01011011 # Z\n01011011 00111001 # [\n01011100 00110001 # \\\n01011101 00001111 # ]\n01011110 01100011 # ^\n01011111 00001000 # _\n01100000 00000010 # `\n01100001 01110111 # a\n01100010 01111100 # b\n01100011 01011000 # c\n01100100 01011110 # d\n01100101 01111001 # e\n01100110 01110001 # f\n01100111 01101111 # g\n01101000 01110100 # h\n01101001 00000100 # i\n01101010 00001110 # j\n01101011 01110110 # k\n01101100 00110000 # l\n01101101 00010100 # m\n01101110 01010100 # n\n01101111 01011100 # o\n01110000 01110011 # p\n01110001 01100111 # q\n01110010 01010000 # r\n01110011 01101101 # s\n01110100 01111000 # t\n01110101 00011100 # u\n01110110 00011100 # v\n01110111 00101010 # w\n01111000 01110110 # x\n01111001 01101110 # y\n01111010 01011011 # z\n01111011 00111001 # {\n01111100 00000110 # |\n01111101 00001111 # }\n01111110 01000000 # ~\n01111111 00000000 # DEL\n10000000 11000000 # Ç\n10000001 11111001 # ü\n10000010 10100100 # é\n10000011 10110000 # â\n10000100 10011001 # ä\n10000101 10001010 # à\n10000100 10011001 # ä\n10000101 10001010 # à\n10000110 10000110 # å\n10000111 11001110 # ç\n10001000 10100000 # ê\n10001001 10010010 # ë\n10001010 10001000 # è\n10001011 10010100 # ï\n10001100 11000110 # î\n10001101 11010000 # ì\n10001110 10101011 # Ä\n10001111 10011100 # Å\n10010000 10001110 # É\n10010001 11111000 # æ\n10010010 11111101 # Æ\n10010011 10011100 # ô\n10010100 10010000 # ö\n10010101 11000000 # ò\n10010110 11110000 # û\n10010111 11000000 # ù\n10011000 10001001 # ÿ\n10011001 01101110 # Ö\n10011010 01111001 # Ü\n10011011 11000110 # ¢\n10011100 10100011 # £\n10011101 10010001 # ¥\n10011110 01011100 # ₧\n10011111 01110011 # ƒ\n10100000 00000000 #  \n10100001 10000110 # ¡\n10100010 01011110 # ¢\n10100011 10100011 # £\n10100100 10010001 # ¤\n10100101 10010001 # ¥\n10100110 00000110 # ¦\n10100111 01001111 # §\n10101000 00100010 # ¨\n10101001 01110111 # ©\n10101010 00011110 # ª\n10101011 01100000 # «\n10101100 01000000 # ¬\n10101101 10000000 # ­\n10101110 01110111 # ®\n10101111 01000000 # ¯\n10110000 01100011 # °\n10110001 01000000 # ±\n10110010 01011011 # ²\n10110011 01001111 # ³\n10110100 00000010 # ´\n10110101 01111100 # µ\n10110110 01011110 # ¶\n10110111 10000000 # ·\n10111000 00000010 # ¸\n10111001 00000110 # ¹\n10111010 00011110 # º\n10111011 01000010 # »\n10111100 01100110 # ¼\n10111101 01101101 # ½\n10111110 01111101 # ¾\n10111111 11010011 # ¿\n11000000 01110111 # À\n11000001 01110111 # Á\n11000010 01110111 # Â\n11000011 01110111 # Ã\n11000100 01110111 # Ä\n11000101 01110111 # Å\n11000110 11111101 # Æ\n11000111 00111001 # Ç\n11001000 01111001 # È\n11001001 01111001 # É\n11001010 01111001 # Ê\n11001011 01111001 # Ë\n11001100 00000110 # Ì\n11001101 00000110 # Í\n11001110 00000110 # Î\n11001111 00000110 # Ï\n11010000 01111110 # Ð\n11010001 01010100 # Ñ\n11010010 00111111 # Ò\n11010011 00111111 # Ó\n11010100 00111111 # Ô\n11010101 00111111 # Õ\n11010110 00111111 # Ö\n11010111 01000000 # ×\n11011000 00111111 # Ø\n11011001 00111110 # Ù\n11011010 00111110 # Ú\n11011011 00111110 # Û\n11011100 00111110 # Ü\n11011101 01101110 # Ý\n11011110 01110010 # Þ\n11011111 01111101 # ß\n11100000 01110111 # à\n11100001 01110111 # á\n11100010 01110111 # â\n11100011 01110111 # ã\n11100100 01110111 # ä\n11100100 01110111 # ä\n11100101 01110111 # å\n11100110 11111001 # æ\n11100111 01011000 # ç\n11101000 01111001 # è\n11101001 01111001 # é\n11101010 01111001 # ê\n11101011 01111001 # ë\n11101100 00000100 # ì\n11101101 00000100 # í\n11101110 00000100 # î\n11101111 00000100 # ï\n11110000 01111101 # ð\n11110001 01010100 # ñ\n11110010 01011100 # ò\n11110011 01011100 # ó\n11110100 01011100 # ô\n11110101 01011100 # õ\n11110110 01011100 # ö\n11110111 01000000 # ÷\n11111000 01011100 # ø\n11111001 00011100 # ù\n11111010 00011100 # ú\n11111011 00011100 # û\n11111100 00011100 # ü\n11111101 01101110 # ý\n11111110 01110010 # þ\n11111111 00011100 # ÿ")) pla_3 (
    .in(register_1_q[15:8]), .out(pla_3_out));
  PLA #(.in_width(8), .out_width(8), .\table ("00000000 00000000 # NULL\n00000001 00000000 # SOH\n00000010 00000000 # STX\n00000011 00000000 # ETX\n00000100 00000000 # EOT\n00000101 00000000 # ENQ\n00000110 00000000 # ACK\n00000111 00000000 # BEL\n00001000 00000000 # BS\n00001001 00000000 # TAB\n00001010 00000000 # LF\n00001011 00000000 # VT\n00001100 00000000 # FF\n00001101 00000000 # CR\n00001110 00000000 # SO\n00001111 00000000 # SI\n00010000 00000000 # DLE\n00010001 00000000 # DC1\n00010010 00000000 # DC2\n00010011 00000000 # DC3\n00010100 00000000 # DC4\n00010101 00000000 # NAK\n00010110 00000000 # SYN\n00010111 00000000 # ETB\n00011000 00000000 # CAN\n00011001 00000000 # EM\n00011010 00000000 # SUB\n00011011 00000000 # ESC\n00011100 00000000 # FS\n00011101 00000000 # GS\n00011110 00000000 # RS\n00011111 00000000 # US\n00100000 00000000 # Space\n00100001 10000110 # !\n00100010 00100010 # \"\n00100011 01100110 # #\n00100100 01101101 # $\n00100101 01001001 # %\n00100110 01111111 # &\n00100111 00000010 # '\n00101000 00111001 # (\n00101001 00001111 # )\n00101010 01100011 # *\n00101011 01000000 # +\n00101100 10000000 # ,\n00101101 01000000 # -\n00101110 10000000 # .\n00101111 01010010 # /\n00110000 00111111 # 0\n00110001 00000110 # 1\n00110010 01011011 # 2\n00110011 01001111 # 3\n00110100 01100110 # 4\n00110101 01101101 # 5\n00110100 01100110 # 4\n00110101 01101101 # 5\n00110110 01111101 # 6\n00110111 00000111 # 7\n00111000 01111111 # 8\n00111001 01101111 # 9\n00111010 10000010 # :\n00111011 10000010 # ;\n00111100 01100000 # <\n00111101 01001000 # =\n00111110 01000010 # >\n00111111 11010011 # ?\n01000000 01011111 # @\n01000001 01110111 # A\n01000010 01111111 # B\n01000011 00111001 # C\n01000100 01011110 # D\n01000101 01111001 # E\n01000110 01110001 # F\n01000111 00111101 # G\n01001000 01110110 # H\n01001001 00000110 # I\n01001010 00011110 # J\n01001011 01110110 # K\n01001100 00111000 # L\n01001101 00010101 # M\n01001110 01010100 # N\n01001111 00111111 # O\n01010000 01110011 # P\n01010001 01100111 # Q\n01010010 01010000 # R\n01010011 01101101 # S\n01010100 01111000 # T\n01010101 00111110 # U\n01010110 00011100 # V\n01010111 00101010 # W\n01011000 01110110 # X\n01011001 01101110 # Y\n01011010 01011011 # Z\n01011011 00111001 # [\n01011100 00110001 # \\\n01011101 00001111 # ]\n01011110 01100011 # ^\n01011111 00001000 # _\n01100000 00000010 # `\n01100001 01110111 # a\n01100010 01111100 # b\n01100011 01011000 # c\n01100100 01011110 # d\n01100101 01111001 # e\n01100110 01110001 # f\n01100111 01101111 # g\n01101000 01110100 # h\n01101001 00000100 # i\n01101010 00001110 # j\n01101011 01110110 # k\n01101100 00110000 # l\n01101101 00010100 # m\n01101110 01010100 # n\n01101111 01011100 # o\n01110000 01110011 # p\n01110001 01100111 # q\n01110010 01010000 # r\n01110011 01101101 # s\n01110100 01111000 # t\n01110101 00011100 # u\n01110110 00011100 # v\n01110111 00101010 # w\n01111000 01110110 # x\n01111001 01101110 # y\n01111010 01011011 # z\n01111011 00111001 # {\n01111100 00000110 # |\n01111101 00001111 # }\n01111110 01000000 # ~\n01111111 00000000 # DEL\n10000000 11000000 # Ç\n10000001 11111001 # ü\n10000010 10100100 # é\n10000011 10110000 # â\n10000100 10011001 # ä\n10000101 10001010 # à\n10000100 10011001 # ä\n10000101 10001010 # à\n10000110 10000110 # å\n10000111 11001110 # ç\n10001000 10100000 # ê\n10001001 10010010 # ë\n10001010 10001000 # è\n10001011 10010100 # ï\n10001100 11000110 # î\n10001101 11010000 # ì\n10001110 10101011 # Ä\n10001111 10011100 # Å\n10010000 10001110 # É\n10010001 11111000 # æ\n10010010 11111101 # Æ\n10010011 10011100 # ô\n10010100 10010000 # ö\n10010101 11000000 # ò\n10010110 11110000 # û\n10010111 11000000 # ù\n10011000 10001001 # ÿ\n10011001 01101110 # Ö\n10011010 01111001 # Ü\n10011011 11000110 # ¢\n10011100 10100011 # £\n10011101 10010001 # ¥\n10011110 01011100 # ₧\n10011111 01110011 # ƒ\n10100000 00000000 #  \n10100001 10000110 # ¡\n10100010 01011110 # ¢\n10100011 10100011 # £\n10100100 10010001 # ¤\n10100101 10010001 # ¥\n10100110 00000110 # ¦\n10100111 01001111 # §\n10101000 00100010 # ¨\n10101001 01110111 # ©\n10101010 00011110 # ª\n10101011 01100000 # «\n10101100 01000000 # ¬\n10101101 10000000 # ­\n10101110 01110111 # ®\n10101111 01000000 # ¯\n10110000 01100011 # °\n10110001 01000000 # ±\n10110010 01011011 # ²\n10110011 01001111 # ³\n10110100 00000010 # ´\n10110101 01111100 # µ\n10110110 01011110 # ¶\n10110111 10000000 # ·\n10111000 00000010 # ¸\n10111001 00000110 # ¹\n10111010 00011110 # º\n10111011 01000010 # »\n10111100 01100110 # ¼\n10111101 01101101 # ½\n10111110 01111101 # ¾\n10111111 11010011 # ¿\n11000000 01110111 # À\n11000001 01110111 # Á\n11000010 01110111 # Â\n11000011 01110111 # Ã\n11000100 01110111 # Ä\n11000101 01110111 # Å\n11000110 11111101 # Æ\n11000111 00111001 # Ç\n11001000 01111001 # È\n11001001 01111001 # É\n11001010 01111001 # Ê\n11001011 01111001 # Ë\n11001100 00000110 # Ì\n11001101 00000110 # Í\n11001110 00000110 # Î\n11001111 00000110 # Ï\n11010000 01111110 # Ð\n11010001 01010100 # Ñ\n11010010 00111111 # Ò\n11010011 00111111 # Ó\n11010100 00111111 # Ô\n11010101 00111111 # Õ\n11010110 00111111 # Ö\n11010111 01000000 # ×\n11011000 00111111 # Ø\n11011001 00111110 # Ù\n11011010 00111110 # Ú\n11011011 00111110 # Û\n11011100 00111110 # Ü\n11011101 01101110 # Ý\n11011110 01110010 # Þ\n11011111 01111101 # ß\n11100000 01110111 # à\n11100001 01110111 # á\n11100010 01110111 # â\n11100011 01110111 # ã\n11100100 01110111 # ä\n11100100 01110111 # ä\n11100101 01110111 # å\n11100110 11111001 # æ\n11100111 01011000 # ç\n11101000 01111001 # è\n11101001 01111001 # é\n11101010 01111001 # ê\n11101011 01111001 # ë\n11101100 00000100 # ì\n11101101 00000100 # í\n11101110 00000100 # î\n11101111 00000100 # ï\n11110000 01111101 # ð\n11110001 01010100 # ñ\n11110010 01011100 # ò\n11110011 01011100 # ó\n11110100 01011100 # ô\n11110101 01011100 # õ\n11110110 01011100 # ö\n11110111 01000000 # ÷\n11111000 01011100 # ø\n11111001 00011100 # ù\n11111010 00011100 # ú\n11111011 00011100 # û\n11111100 00011100 # ü\n11111101 01101110 # ý\n11111110 01110010 # þ\n11111111 00011100 # ÿ")) pla_4 (
    .in(register_1_q[31:24]), .out(pla_4_out));
  Joystick joystick_1 ();  // open: x, y
  assign {controlled_buffer_1_out_4, controlled_buffer_1_out_3, controlled_buffer_1_out_2, controlled_buffer_1_out} = address_selector_2_read_out ? {not_1_out[7], keyboard_1_data, undriven_3, undriven_2, random_1_out} : 32'bz;  // Controlled_Buffer controlled_buffer_4
  Real_Time_Device real_time_device_1 (
    .Clock(Cl0ck), .Reset(Reset), .Address(address_selector_5_address_out[3:2]),
    .Write(address_selector_5_write_out),
    .Data_In({controlled_buffer_1_out_4, controlled_buffer_1_out_3, controlled_buffer_1_out_2, controlled_buffer_1_out}),
    .Timer_Interrupt(real_time_device_1_timer_interrupt), .Data_Out(real_time_device_1_data_out));
  // DipSwitch dipswitch_1: pin names not known
  _7_Segment_Display u_7_segment_display_1 (
    .g(pla_1_out[6]), .f(pla_1_out[5]), .a(pla_1_out[0]), .b(pla_1_out[1]), .e(pla_1_out[4]),
    .d(pla_1_out[3]), .c(pla_1_out[2]), .dp(pla_1_out[7]));
  _7_Segment_Display u_7_segment_display_2 (
    .g(pla_3_out[6]), .f(pla_3_out[5]), .a(pla_3_out[0]), .b(pla_3_out[1]), .e(pla_3_out[4]),
    .d(pla_3_out[3]), .c(pla_3_out[2]), .dp(pla_3_out[7]));
  Random random_1 (.next(address_selector_2_read_out), .clk(Cl0ck), .out(random_1_out[7:0]));  // open: clr
  _7_Segment_Display u_7_segment_display_3 (
    .g(pla_2_out[6]), .f(pla_2_out[5]), .a(pla_2_out[0]), .b(pla_2_out[1]), .e(pla_2_out[4]),
    .d(pla_2_out[3]), .c(pla_2_out[2]), .dp(pla_2_out[7]));
  _7_Segment_Display u_7_segment_display_4 (
    .g(pla_4_out[6]), .f(pla_4_out[5]), .a(pla_4_out[0]), .b(pla_4_out[1]), .e(pla_4_out[4]),
    .d(pla_4_out[3]), .c(pla_4_out[2]), .dp(pla_4_out[7]));
  TTY #(.cols(64), .rows(12)) tty_1 (.data(controlled_buffer_1_out[6:0]), .clk(Cl0ck), .we(and_1_out), .clr(or_1_out));
  or or_1 (or_1_out, Reset, and_2_out);
  // RGB_Video #(.cursor("No Cursor"), .height(64), .scale(6), .width(64)) rgb_video_1: pin names not known; wires that end beside it: Reset, Cl0ck, address_selector_3_write_out, {controlled_buffer_1_out_3, controlled_buffer_1_out_2, controlled_buffer_1_out}

  // Notes on the sheet:
  //   <Processor     Input Output Devices>
  //   Data Bus
  //   (IO Bus)
  //   Address Bus
  //   contents of Trap_Handler (hex, n*v repeats v):
  //   6f 0 0 4 8*0 6f 0 40 41 12*0 6f 0 c0 42 12*0 6f 0 40 44 16*0 73 10 1 34 13 1 0 fc 23 20 11 0 23 22
  //   d1 0 23 24 e1 0 23 28 f1 0 23 2c 51 0 23 2e 61 0 23 20 71 2 f3 27 20 34 93 f7 f7 7f 13 7 b0 0 63 66
  //   f7 4 13 97 27 0 97 7 0 0 93 87 47 1 b3 87 e7 0 83 a7 7 0 67 80 7 0 cc 0 0 80 bc 0 0 80 d0 0 0 80 d4
  //   0 0 80 a8 3 0 80 bc 0 0 80 ac 3 0 80 bc 0 0 80 b0 3 0 80 bc 0 0 80 bc 0 0 80 b0 3 0 80 17 5 0 0 13 5
  //   85 46 ef 0 40 3d 6f 0 0 0 6f 0 40 32 6f 0 0 32 93 6 5 0 17 5 0 0 13 5 c5 4a ef 0 80 3b 17 5 0 0 13 5
  //   5 53 ef 0 c0 3a 3 25 1 0 ef 0 80 3c 17 5 0 0 13 5 45 52 ef 0 80 39 73 25 0 34 ef 0 40 3b 17 5 0 0 13
  //   5 85 51 ef 0 40 38 13 85 1 0 ef 0 0 3a 17 5 0 0 13 5 c5 50 ef 0 0 37 13 5 2 0 ef 0 c0 38 17 5 0 0 13
  //   5 5 50 ef 0 c0 35 3 25 81 1 ef 0 80 37 17 5 0 0 13 5 45 4f ef 0 80 34 3 25 c1 1 ef 0 40 36 17 5 0 0
  //   13 5 85 4e ef 0 40 33 3 25 1 2 ef 0 0 35 17 5 0 0 13 5 c5 4d ef 0 0 32 13 5 4 0 ef 0 c0 33 17 5 0 0
  //   13 5 5 4d ef 0 c0 30 13 85 4 0 ef 0 80 32 17 5 0 0 13 5 45 4c ef 0 80 2f 13 85 6 0 ef 0 40 31 17 5 0
  //   0 13 5 85 4b ef 0 40 2e 13 85 5 0 ef 0 0 30 17 5 0 0 13 5 c5 4a ef 0 0 2d 13 5 6 0 ef 0 c0 2e 17 5 0
  //   0 13 5 5 4a ef 0 c0 2b 3 25 41 0 ef 0 80 2d 17 5 0 0 13 5 45 49 ef 0 80 2a 3 25 81 0 ef 0 40 2c 17 5
  //   0 0 13 5 85 48 ef 0 40 29 3 25 1 1 ef 0 0 2b 17 5 0 0 13 5 c5 47 ef 0 0 28 13 5 8 0 ef 0 c0 29 17 5
  //   0 0 13 5 5 47 ef 0 c0 26 13 85 8 0 ef 0 80 28 17 5 0 0 13 5 45 46 ef 0 80 25 13 5 9 0 ef 0 40 27 17
  //   5 0 0 13 5 85 45 ef 0 40 24 13 85 9 0 ef 0 0 26 17 5 0 0 13 5 c5 44 ef 0 0 23 13 5 a 0 ef 0 c0 24 17
  //   5 0 0 13 5 5 44 ef 0 c0 21 13 85 a 0 ef 0 80 23 17 5 0 0 13 5 45 43 ef 0 80 20 13 5 b 0 ef 0 40 22
  //   17 5 0 0 13 5 85 42 ef 0 40 1f 13 85 b 0 ef 0 0 21 17 5 0 0 13 5 c5 41 ef 0 0 1e 13 5 c 0 ef 0 c0 1f
  //   17 5 0 0 13 5 5 41 ef 0 c0 1c 13 85 c 0 ef 0 80 1e 17 5 0 0 13 5 45 40 ef 0 80 1b 13 5 d 0 ef 0 40
  //   1d 17 5 0 0 13 5 85 3f ef 0 40 1a 13 85 d 0 ef 0 0 1c 17 5 0 0 13 5 c5 3e ef 0 0 19 13 5 e 0 ef 0 c0
  //   1a 17 5 0 0 13 5 5 3e ef 0 c0 17 13 85 e 0 ef 0 80 19 17 5 0 0 13 5 45 3d ef 0 80 16 13 5 f 0 ef 0
  //   40 18 17 5 0 0 13 5 85 3c ef 0 40 15 13 85 f 0 ef 0 0 17 17 5 0 0 13 5 c5 3b ef 0 0 14 73 25 10 34
  //   ef 0 c0 15 17 5 0 0 13 5 45 3b ef 0 c0 12 73 25 0 30 ef 0 80 14 17 5 0 0 13 5 5 3b ef 0 80 11 73 25
  //   40 30 ef 0 40 13 17 5 0 0 13 5 85 3a ef 0 40 10 73 25 40 34 ef 0 0 12 13 85 6 0 6f 0 c0 4 6f 0 80 4
  //   6f 0 40 4 93 2 0 0 63 18 55 0 93 86 5 0 ef 0 c0 d 6f 0 0 3 93 2 10 0 63 16 55 0 23 22 b1 2 6f 0 0 2
  //   93 2 20 0 63 16 55 0 23 24 b1 2 6f 0 0 1 93 2 30 0 63 14 55 0 23 26 b1 2 f3 22 10 34 93 82 42 0 73
  //   90 12 34 83 20 1 0 83 26 41 0 3 27 81 0 83 27 1 1 83 22 81 1 3 23 c1 1 83 23 1 2 73 21 0 34 73 0 20
  //   30 73 10 1 34 13 1 0 fc 23 20 51 0 23 22 11 0 83 22 41 2 e7 80 2 0 83 22 1 0 83 20 41 0 73 21 0 34
  //   73 0 20 30 73 10 1 34 13 1 0 fc 23 20 51 0 23 22 11 0 83 22 81 2 e7 80 2 0 83 22 1 0 83 20 41 0 73
  //   21 0 34 73 0 20 30 73 10 1 34 13 1 0 fc 23 20 51 0 23 22 11 0 83 22 c1 2 e7 80 2 0 83 22 1 0 83 20
  //   41 0 73 21 0 34 73 0 20 30 93 2 5 0 97 3 10 81 93 83 43 b6 3 83 2 0 23 80 63 0 63 6 3 0 93 82 12 0
  //   6f f0 1f ff 67 80 0 0 13 1 41 ff 23 20 11 0 23 22 81 0 23 24 91 0 13 4 5 0 93 4 c0 1 63 c0 4 2 33 55
  //   94 0 13 75 f5 0 ef 0 c0 2 b7 2 10 1 23 80 a2 0 93 84 c4 ff 6f f0 5f fe 13 5 4 0 83 20 1 0 3 24 41 0
  //   83 24 81 0 13 1 c1 0 67 80 0 0 93 2 a0 0 63 56 55 0 13 5 5 3 67 80 0 0 13 5 75 3 67 80 0 0 46 61 74
  //   61 6c 20 65 72 72 6f 72 3a 20 63 61 75 73 65 20 75 6e 6b 6e 6f 77 6e 0 0 65 72 72 6f 72 3a 20 69 6e
  //   73 74 72 75 63 74 69 6f 6e 20 61 64 64 72 65 73 73 20 6d 69 73 61 6c 69 67 6e 65 64 0 0 0 65 72 72
  //   6f 72 3a 20 69 6c 6c 65 67 61 6c 20 69 6e 73 74 72 75 63 74 69 6f 6e 0 0 42 72 65 61 6b 70 6f 69 6e
  //   74 20 72 65 61 63 68 65 64 a 0 65 72 72 6f 72 3a 20 6c 6f 61 64 20 61 64 64 72 65 73 73 20 6d 69 73
  //   61 6c 69 67 6e 65 64 0 0 65 72 72 6f 72 3a 20 73 74 6f 72 65 20 61 64 64 72 65 73 73 20 6d 69 73 61
  //   6c 69 67 6e 65 64 0 45 6e 76 69 72 6f 6e 6d 65 6e 74 20 63 61 6c 6c 20 66 72 6f 6d 20 75 73 65 72 0
  //   0 45 6e 76 69 72 6f 6e 6d 65 6e 74 20 63 61 6c 6c 20 66 72 6f 6d 20 6d 61 63 68 69 6e 65 0 0 0 a 72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
  //   Keyboard
  //   Joystick
  //   Switches
endmodule

module ALU (
  input  [4:0] Operation,
  input  Use_PC,
  input  [31:0] a,
  input  [31:0] Program_Counter_In,
  input  Use_Immediate,
  input  [31:0] b,
  input  [31:0] Immediate,
  output [3:0] CNZV,
  output [31:0] Result
);

  wire and_1_out, comparator_1_lt, comparator_2_lt, or_1_out, xnor_1_out, xor_2_out, xor_3_out;
  wire [1:0] and_3_out;
  wire [1:1] and_2_out;
  wire [31:0] adder_subtractor_1_r, and_4_out, bit_extender_1_out, bit_extender_2_out, divider_1_out,
       divider_1_rem, divider_2_out, divider_2_rem, multiplexer_1_out, multiplexer_2_out, multiplexer_3_out,
       multiplication_1_r_high, multiplication_1_r_low, or_2_out, shifter_1_out, shifter_2_out,
       shifter_3_out, xor_1_out;

  or or_1 (or_1_out, Operation[2], ~Operation[4]);  // OR_Gate
  and and_1 (and_1_out, Operation[0], ~Operation[1], ~Operation[3], or_1_out);  // AND_Gate
  Multiplexer #(.width(32)) multiplexer_1 (.in0(a), .in1(Program_Counter_In), .out(multiplexer_1_out), .sel(Use_PC));
  Multiplexer #(.width(32)) multiplexer_2 (.in0(b), .in1(Immediate), .out(multiplexer_2_out), .sel(Use_Immediate));
  and and_2 (and_2_out[1], ~and_1_out, Use_Immediate);  // AND_Gate
  assign and_3_out = Operation[4:3] & ~{2{and_2_out[1]}};  // AND_Gate and_3, 2 bits wide
  assign or_2_out = multiplexer_1_out | multiplexer_2_out;  // OR_Gate or_2, 32 bits wide
  assign and_4_out = multiplexer_1_out & multiplexer_2_out;  // AND_Gate and_4, 32 bits wide
  Adder_Subtractor adder_subtractor_1 (
    .Subraction(and_3_out[1]), .A(multiplexer_1_out), .B(multiplexer_2_out), .R(adder_subtractor_1_r),
    .C_Out(CNZV[0]));
  Shifter #(.width(32)) shifter_1 (.in(multiplexer_1_out), .\dist (multiplexer_2_out[4:0]), .out(shifter_1_out));
  assign bit_extender_1_out = {{31{1'b0}}, comparator_1_lt};  // Bit_Extender bit_extender_1
  Comparator #(.width(32)) comparator_1 (
    .a(multiplexer_1_out), .b(multiplexer_2_out), .lt(comparator_1_lt));  // open: gt, eq
  assign bit_extender_2_out = {{31{1'b0}}, comparator_2_lt};  // Bit_Extender bit_extender_2
  Comparator #(.mode("unsigned"), .width(32)) comparator_2 (
    .a(multiplexer_1_out), .b(multiplexer_2_out), .lt(comparator_2_lt));  // open: gt, eq
  assign xor_1_out = multiplexer_1_out ^ multiplexer_2_out;  // XOR_Gate xor_1, 32 bits wide
  Shifter #(.shift("lr"), .width(32)) shifter_2 (
    .in(multiplexer_1_out), .\dist (multiplexer_2_out[4:0]), .out(shifter_2_out));
  Shifter #(.shift("ar"), .width(32)) shifter_3 (
    .in(multiplexer_1_out), .\dist (multiplexer_2_out[4:0]), .out(shifter_3_out));
  Multiplication multiplication_1 (
    .Sign(Operation[1:0]), .A(multiplexer_1_out), .B(multiplexer_2_out), .R_Low(multiplication_1_r_low),
    .R_High(multiplication_1_r_high));
  Divider #(.mode("twosComplement"), .width(32)) divider_1 (
    .a(multiplexer_1_out), .b(multiplexer_2_out), .out(divider_1_out), .rem(divider_1_rem));  // open: upper
  Divider #(.width(32)) divider_2 (
    .a(multiplexer_1_out), .b(multiplexer_2_out), .out(divider_2_out), .rem(divider_2_rem));  // open: upper
  Multiplexer #(.width(32)) multiplexer_3 (
    .in0(shifter_2_out), .in1(shifter_3_out), .out(multiplexer_3_out), .sel(and_3_out[1]));
  Multiplexer #(.select(4), .width(32)) multiplexer_4 (
    .in0(adder_subtractor_1_r), .in1(shifter_1_out), .in2(bit_extender_1_out), .in3(bit_extender_2_out),
    .in4(xor_1_out), .in5(multiplexer_3_out), .in6(or_2_out), .in7(and_4_out), .in8(multiplication_1_r_low),
    .in9(multiplication_1_r_high), .in10(multiplication_1_r_high), .in11(multiplication_1_r_high),
    .in12(divider_1_out), .in13(divider_2_out), .in14(divider_1_rem), .in15(divider_2_rem),
    .out({CNZV[1], Result[30:0]}), .sel({and_3_out[0], Operation[2:0]}));
  xor xor_2 (xor_2_out, CNZV[1], multiplexer_1_out[31]);
  xnor xnor_1 (xnor_1_out, multiplexer_1_out[31], multiplexer_2_out[31]);
  nor nor_1 (CNZV[2], Result[0], Result[1], Result[2], Result[3], Result[4], Result[5], Result[6], Result[7], Result[8], Result[9], Result[10], Result[11], Result[12], Result[13], Result[14], Result[15], Result[16], Result[17], Result[18], Result[19], Result[20], Result[21], Result[22], Result[23], Result[24], Result[25], Result[26], Result[27], Result[28], Result[29], Result[30], CNZV[1]);
  xor xor_3 (xor_3_out, xnor_1_out, and_3_out[1]);
  and and_5 (CNZV[3], xor_2_out, xor_3_out);

  assign Result[31] = CNZV[1];

  // Notes on the sheet:
  //   a: initial=0xffffffff
endmodule

module Program_Counter (
  input  Write,
  input  Jump,
  input  System_Jump,
  input  Reset,
  input  Clock,
  input  PC_Relative,
  input  [31:0] Address_In,
  input  [31:0] Immediate,
  input  Use_Offset,
  input  [31:0] System_Target_Address,
  input  System_Load,
  input  Forward_Address,
  output [31:0] Current_Out,
  output [31:0] Next_Out,
  output [31:0] Calculated_Address,
  output [31:0] Address_Bus_Out,
  output [1:0] Byte_Offset
);

  wire decoder_1_out0, decoder_1_out1, or_1_out;
  wire [1:0] and_1_out;
  wire [31:0] multiplexer_1_out, multiplexer_2_out, multiplexer_3_out;

  Multiplexer #(.width(32)) multiplexer_1 (
    .in0(Address_In), .in1({Current_Out[31:2], 2'b00}), .out(multiplexer_1_out), .sel(PC_Relative));
  Adder #(.width(32)) adder_1 (.a(multiplexer_1_out), .b(Immediate), .out(Calculated_Address));  // open: cin, cout
  or or_1 (or_1_out, Jump, System_Jump);
  Multiplexer #(.width(32)) multiplexer_2 (
    .in0(Calculated_Address), .in1(System_Target_Address), .out(multiplexer_2_out), .sel(System_Jump));
  Decoder decoder_1 (.out0(decoder_1_out0), .out1(decoder_1_out1), .sel(or_1_out), .en(Write));
  Counter #(.max('h3fffffff), .width(30)) Next_PC (
    .load(decoder_1_out1), .D(multiplexer_2_out[31:2]), .count(decoder_1_out0), .Q(Next_Out[31:2]),
    .clk(Clock), .clr(Reset));  // open: carry, up
  assign and_1_out = multiplexer_2_out[1:0] & {2{Use_Offset}};  // AND_Gate and_1, 2 bits wide
  Register #(.width(30)) Current (.D(Next_Out[31:2]), .en(Write), .clk(Clock), .Q(Current_Out[31:2]), .clr(Reset));
  Multiplexer #(.width(32)) multiplexer_3 (
    .in0({multiplexer_2_out[31:2], and_1_out}), .in1(System_Target_Address), .out(multiplexer_3_out),
    .sel(System_Load));
  Multiplexer #(.width(32)) multiplexer_4 (
    .in0({Next_Out[31:2], 2'b00}), .in1(multiplexer_3_out), .out(Address_Bus_Out), .sel(Forward_Address));
  Register #(.width(2)) Byte_Offset_Reg (
    .D(multiplexer_2_out[1:0]), .en(Forward_Address), .clk(Clock), .Q(Byte_Offset), .clr(Reset));

  assign Current_Out[1:0] = 2'b00;
  assign Next_Out[1:0] = 2'b00;

  // Other names for the same wires on the sheet: Current_PC[31:2] = Current_Out[31:2]
endmodule

module Input_Buffer (
  input  [2:0] Data_Type,
  input  [1:0] Data_Offset,
  input  [31:0] IO_In,
  input  Write,
  input  Clock,
  output [31:0] CPU_Out
);

  wire and_1_out, and_2_out, not_1_out;
  wire [7:0] Input_Register_q, Input_Register_q_2, Input_Register_q_3, Input_Register_q_4, multiplexer_1_out;
  wire [15:0] multiplexer_2_out, multiplexer_3_out;
  wire [31:0] bit_extender_1_out, bit_extender_2_out, multiplexer_4_out;

  Register #(.width(32)) Input_Register (
    .D(IO_In), .en(Write), .clk(Clock),
    .Q({Input_Register_q_4, Input_Register_q_3, Input_Register_q_2, Input_Register_q}));  // open: clr
  Multiplexer #(.select(2), .width(8)) multiplexer_1 (
    .in0(Input_Register_q), .in1(Input_Register_q_2), .in2(Input_Register_q_3), .in3(Input_Register_q_4),
    .out(multiplexer_1_out), .sel(Data_Offset));
  Multiplexer #(.width(16)) multiplexer_2 (
    .in0({Input_Register_q_2, Input_Register_q}), .in1({Input_Register_q_3, Input_Register_q_2}),
    .out(multiplexer_2_out), .sel(Data_Offset[0]));
  Multiplexer #(.width(16)) multiplexer_3 (
    .in0(multiplexer_2_out), .in1({Input_Register_q_4, Input_Register_q_3}), .out(multiplexer_3_out),
    .sel(Data_Offset[1]));
  not not_1 (not_1_out, Data_Type[2]);
  and and_1 (and_1_out, multiplexer_1_out[7], not_1_out);
  assign bit_extender_1_out = {{24{and_1_out}}, multiplexer_1_out};  // Bit_Extender bit_extender_1
  and and_2 (and_2_out, multiplexer_3_out[15], not_1_out);
  assign bit_extender_2_out = {{16{and_2_out}}, multiplexer_3_out};  // Bit_Extender bit_extender_2
  Multiplexer #(.width(32)) multiplexer_4 (
    .in0(bit_extender_1_out), .in1(bit_extender_2_out), .out(multiplexer_4_out), .sel(Data_Type[0]));
  Multiplexer #(.width(32)) multiplexer_5 (
    .in0(multiplexer_4_out),
    .in1({Input_Register_q_4, Input_Register_q_3, Input_Register_q_2, Input_Register_q}), .out(CPU_Out),
    .sel(Data_Type[1]));

  // Notes on the sheet:
  //   IO_In: initial=0xf2f2f2f2
endmodule

module Register_File (
  input  [14:0] Addresses_In,
  input  [31:0] C_Bus_In,
  input  Write,
  input  Clock,
  input  Reset,
  output [31:0] A_Bus_Out,
  output [31:0] B_Bus_Out
);

  Register_Bank IntRegisterBank (
    .Address_A(Addresses_In[9:5]), .Address_B(Addresses_In[14:10]), .Data_In(C_Bus_In), .Clock(Clock),
    .Address_C(Addresses_In[4:0]), .Write_Enable(Write), .Reset(Reset), .A_Data_Out(A_Bus_Out),
    .B_Data_Out(B_Bus_Out));
endmodule

module Register_Bank (
  input  [4:0] Address_A,
  input  Reset,
  input  [31:0] Data_In,
  input  Clock,
  input  [4:0] Address_C,
  input  [4:0] Address_B,
  input  Write_Enable,
  output [31:0] A_Data_Out,
  output [31:0] B_Data_Out
);

  wire [31:0] decoder_1_out0, x1_q, x2_q, x3_q, x4_q, x5_q, x6_q, x7_q, x8_q, x9_q, x10_q, x11_q, x12_q,
       x13_q, x14_q, x15_q, x16_q, x17_q, x18_q, x19_q, x20_q, x21_q, x22_q, x23_q, x24_q, x25_q, x26_q,
       x27_q, x28_q, x29_q, x30_q, x31_q;

  Decoder #(.select(5)) decoder_1 (
    .out0(decoder_1_out0[0]), .out1(decoder_1_out0[1]), .out2(decoder_1_out0[2]), .out3(decoder_1_out0[3]),
    .out4(decoder_1_out0[4]), .out5(decoder_1_out0[5]), .out6(decoder_1_out0[6]), .out7(decoder_1_out0[7]),
    .out8(decoder_1_out0[8]), .out9(decoder_1_out0[9]), .out10(decoder_1_out0[10]),
    .out11(decoder_1_out0[11]), .out12(decoder_1_out0[12]), .out13(decoder_1_out0[13]),
    .out14(decoder_1_out0[14]), .out15(decoder_1_out0[15]), .out16(decoder_1_out0[16]),
    .out17(decoder_1_out0[17]), .out18(decoder_1_out0[18]), .out19(decoder_1_out0[19]),
    .out20(decoder_1_out0[20]), .out21(decoder_1_out0[21]), .out22(decoder_1_out0[22]),
    .out23(decoder_1_out0[23]), .out24(decoder_1_out0[24]), .out25(decoder_1_out0[25]),
    .out26(decoder_1_out0[26]), .out27(decoder_1_out0[27]), .out28(decoder_1_out0[28]),
    .out29(decoder_1_out0[29]), .out30(decoder_1_out0[30]), .out31(decoder_1_out0[31]), .sel(Address_C),
    .en(Write_Enable));
  // NoConnect on Data_In
  // NoConnect on decoder_1_out0[0]
  // NoConnect on Clock
  Register #(.width(32)) x2 (.D(Data_In), .en(decoder_1_out0[2]), .clk(Clock), .Q(x2_q), .clr(Reset));
  Register #(.width(32)) x4 (.D(Data_In), .en(decoder_1_out0[4]), .clk(Clock), .Q(x4_q), .clr(Reset));
  Register #(.width(32)) x6 (.D(Data_In), .en(decoder_1_out0[6]), .clk(Clock), .Q(x6_q), .clr(Reset));
  Register #(.width(32)) x8 (.D(Data_In), .en(decoder_1_out0[8]), .clk(Clock), .Q(x8_q), .clr(Reset));
  Register #(.width(32)) x10 (.D(Data_In), .en(decoder_1_out0[10]), .clk(Clock), .Q(x10_q), .clr(Reset));
  Register #(.width(32)) x12 (.D(Data_In), .en(decoder_1_out0[12]), .clk(Clock), .Q(x12_q), .clr(Reset));
  Register #(.width(32)) x14 (.D(Data_In), .en(decoder_1_out0[14]), .clk(Clock), .Q(x14_q), .clr(Reset));
  Register #(.width(32)) x16 (.D(Data_In), .en(decoder_1_out0[16]), .clk(Clock), .Q(x16_q), .clr(Reset));
  Register #(.width(32)) x18 (.D(Data_In), .en(decoder_1_out0[18]), .clk(Clock), .Q(x18_q), .clr(Reset));
  Register #(.width(32)) x20 (.D(Data_In), .en(decoder_1_out0[20]), .clk(Clock), .Q(x20_q), .clr(Reset));
  Register #(.width(32)) x22 (.D(Data_In), .en(decoder_1_out0[22]), .clk(Clock), .Q(x22_q), .clr(Reset));
  Register #(.width(32)) x24 (.D(Data_In), .en(decoder_1_out0[24]), .clk(Clock), .Q(x24_q), .clr(Reset));
  Register #(.width(32)) x26 (.D(Data_In), .en(decoder_1_out0[26]), .clk(Clock), .Q(x26_q), .clr(Reset));
  Register #(.width(32)) x28 (.D(Data_In), .en(decoder_1_out0[28]), .clk(Clock), .Q(x28_q), .clr(Reset));
  Register #(.width(32)) x30 (.D(Data_In), .en(decoder_1_out0[30]), .clk(Clock), .Q(x30_q), .clr(Reset));
  Register #(.width(32)) x1 (.D(Data_In), .en(decoder_1_out0[1]), .clk(Clock), .Q(x1_q), .clr(Reset));
  Register #(.width(32)) x3 (.D(Data_In), .en(decoder_1_out0[3]), .clk(Clock), .Q(x3_q), .clr(Reset));
  Register #(.width(32)) x5 (.D(Data_In), .en(decoder_1_out0[5]), .clk(Clock), .Q(x5_q), .clr(Reset));
  Register #(.width(32)) x7 (.D(Data_In), .en(decoder_1_out0[7]), .clk(Clock), .Q(x7_q), .clr(Reset));
  Register #(.width(32)) x9 (.D(Data_In), .en(decoder_1_out0[9]), .clk(Clock), .Q(x9_q), .clr(Reset));
  Register #(.width(32)) x11 (.D(Data_In), .en(decoder_1_out0[11]), .clk(Clock), .Q(x11_q), .clr(Reset));
  Register #(.width(32)) x13 (.D(Data_In), .en(decoder_1_out0[13]), .clk(Clock), .Q(x13_q), .clr(Reset));
  Register #(.width(32)) x15 (.D(Data_In), .en(decoder_1_out0[15]), .clk(Clock), .Q(x15_q), .clr(Reset));
  Register #(.width(32)) x17 (.D(Data_In), .en(decoder_1_out0[17]), .clk(Clock), .Q(x17_q), .clr(Reset));
  Register #(.width(32)) x19 (.D(Data_In), .en(decoder_1_out0[19]), .clk(Clock), .Q(x19_q), .clr(Reset));
  Register #(.width(32)) x21 (.D(Data_In), .en(decoder_1_out0[21]), .clk(Clock), .Q(x21_q), .clr(Reset));
  Register #(.width(32)) x23 (.D(Data_In), .en(decoder_1_out0[23]), .clk(Clock), .Q(x23_q), .clr(Reset));
  Register #(.width(32)) x25 (.D(Data_In), .en(decoder_1_out0[25]), .clk(Clock), .Q(x25_q), .clr(Reset));
  Register #(.width(32)) x27 (.D(Data_In), .en(decoder_1_out0[27]), .clk(Clock), .Q(x27_q), .clr(Reset));
  Register #(.width(32)) x29 (.D(Data_In), .en(decoder_1_out0[29]), .clk(Clock), .Q(x29_q), .clr(Reset));
  Register #(.width(32)) x31 (.D(Data_In), .en(decoder_1_out0[31]), .clk(Clock), .Q(x31_q), .clr(Reset));
  Multiplexer #(.select(5), .width(32)) multiplexer_1 (
    .in0({32{1'b0}}), .in1(x1_q), .in2(x2_q), .in3(x3_q), .in4(x4_q), .in5(x5_q), .in6(x6_q), .in7(x7_q),
    .in8(x8_q), .in9(x9_q), .in10(x10_q), .in11(x11_q), .in12(x12_q), .in13(x13_q), .in14(x14_q),
    .in15(x15_q), .in16(x16_q), .in17(x17_q), .in18(x18_q), .in19(x19_q), .in20(x20_q), .in21(x21_q),
    .in22(x22_q), .in23(x23_q), .in24(x24_q), .in25(x25_q), .in26(x26_q), .in27(x27_q), .in28(x28_q),
    .in29(x29_q), .in30(x30_q), .in31(x31_q), .out(A_Data_Out), .sel(Address_A));
  Multiplexer #(.select(5), .width(32)) multiplexer_2 (
    .in0({32{1'b0}}), .in1(x1_q), .in2(x2_q), .in3(x3_q), .in4(x4_q), .in5(x5_q), .in6(x6_q), .in7(x7_q),
    .in8(x8_q), .in9(x9_q), .in10(x10_q), .in11(x11_q), .in12(x12_q), .in13(x13_q), .in14(x14_q),
    .in15(x15_q), .in16(x16_q), .in17(x17_q), .in18(x18_q), .in19(x19_q), .in20(x20_q), .in21(x21_q),
    .in22(x22_q), .in23(x23_q), .in24(x24_q), .in25(x25_q), .in26(x26_q), .in27(x27_q), .in28(x28_q),
    .in29(x29_q), .in30(x30_q), .in31(x31_q), .out(B_Data_Out), .sel(Address_B));
endmodule

module Operation_Controller (
  input  Phase1,
  input  Phase2,
  input  [31:0] Data_In,
  input  Exception,
  input  Clock,
  input  Reset,
  input  Next_System_Load,
  input  System_Jump,
  input  [3:0] CNZV,
  output ALU_Use_PC,
  output [31:0] Current_Instruction_Out,
  output Register_File_Write,
  output [14:0] Register_Addresses,
  output ALU_Use_Immediate,
  output [4:0] ALU_OP_Function,
  output [2:0] Data_Type_Out,
  output Load_Upper_Immediate,
  output [31:0] Next_Instruction_Out,
  output [9:0] Next_Decoded_Instruction,
  output Load_Out,
  output Input_Buffer_Read,
  output PAD_Write,
  output Input_Buffer_Write,
  output PAD_Read,
  output Jump,
  output Store_Out,
  output [1:0] PAD_Data_Size,
  output PC_Read_Next,
  output [31:0] Immediate_Out,
  output PC_Relative,
  output PC_Forward_Address
);

  wire and_1_out, and_6_out, and_7_out, Branch_q, Flush, Last_Load, Load, LUI_q, multiplexer_4_out,
       not_2_out, not_3_out, not_4_out, Not_Exception, or_1_out, or_2_out, or_3_out, or_4_out, or_5_out,
       or_6_out, or_7_out, or_8_out, or_12_out, Store, Unconditional_Jump_q, Write_C_q, xor_1_out;
  wire [2:0] Next_Funct3;
  wire [4:0] Last_C_Address_q, multiplexer_5_out;
  wire [6:0] Next_Funct7;
  wire [24:0] multiplexer_2_out;
  wire [31:0] ImmediateDecoder_immediate, multiplexer_1_out;

  Multiplexer #(.width(32)) multiplexer_1 (.in0(Data_In), .in1(32'h13), .out(multiplexer_1_out), .sel(Reset));
  Register #(.width(32)) Next_Instruction (
    .D(multiplexer_1_out), .en(or_1_out), .clk(Clock), .Q(Next_Instruction_Out));  // open: clr
  or or_1 (or_1_out, Phase1, Reset);
  Multiplexer #(.width(32)) multiplexer_2 (
    .in0(Next_Instruction_Out), .in1(32'h13),
    .out({Next_Funct7, multiplexer_2_out[24:15], Next_Funct3, multiplexer_2_out[11:0]}), .sel(or_2_out));
  or or_2 (or_2_out, Reset, Flush);
  Register #(.width(32)) Current_Instuction (
    .D({Next_Funct7, multiplexer_2_out[24:15], Next_Funct3, multiplexer_2_out[11:0]}), .en(Phase2),
    .clk(Clock), .Q(Current_Instruction_Out), .clr(Reset));
  PLA #(.in_width(7), .out_width(10), .\table ("0000011 0000000001 # Load\n0010011 0000010010 # Imm OP\n0010111 0000000100 # AUIPC\n0100011 0000001000 # Store\n0110011 0000010000 # Operation\n0110111 0000100000 # LUI\n1100011 0001000000 # Branch\n1100111 0010000000 # JALR\n1101111 0100000000 # JAL\n1110011 1000000000 # System")) Operation_Decoder (
    .in(multiplexer_2_out[6:0]), .out(Next_Decoded_Instruction));
  or or_3 (or_3_out, Next_Decoded_Instruction[2], Next_Decoded_Instruction[5]);
  Register #(.width(5)) Last_C_Address (
    .D(Current_Instruction_Out[11:7]), .en(Phase2), .clk(Clock), .Q(Last_C_Address_q), .clr(Reset));
  Register #(.width(3)) Last_Data_Type (
    .D(Current_Instruction_Out[14:12]), .en(Phase2), .clk(Clock), .Q(Data_Type_Out), .clr(Reset));
  Immediate_Decoder ImmediateDecoder (
    .Upper_Immediate(or_3_out), .Jump(Next_Decoded_Instruction[8]), .Branch(Next_Decoded_Instruction[6]),
    .Instruction({Next_Funct7, multiplexer_2_out[24:15], Next_Funct3, multiplexer_2_out[11:0]}),
    .Store(Next_Decoded_Instruction[3]), .Immediate(ImmediateDecoder_immediate));
  and and_1 (and_1_out, Last_Load, Phase1);
  Multiplexer #(.width(5)) multiplexer_3 (
    .in0(Current_Instruction_Out[11:7]), .in1(Last_C_Address_q), .out(Register_Addresses[4:0]),
    .sel(and_1_out));
  Register #(.width(32)) Immediate (
    .D(ImmediateDecoder_immediate), .en(Phase2), .clk(Clock), .Q(Immediate_Out), .clr(Reset));
  or or_4 (or_4_out, Next_System_Load, Next_Decoded_Instruction[0]);
  Register #(.width(1)) u_Load (.D(or_4_out), .en(Phase2), .clk(Clock), .Q(Load_Out), .clr(Reset));
  Register #(.width(1)) u_Store (.D(Next_Decoded_Instruction[3]), .en(Phase2), .clk(Clock), .Q(Store_Out), .clr(Reset));
  not not_1 (Not_Exception, Exception);
  and and_2 (Load, Load_Out, Not_Exception);
  and and_3 (Store, Not_Exception, Store_Out);
  Register #(.width(1)) u_Last_Load (.D(Load), .en(Phase2), .clk(Clock), .Q(Last_Load), .clr(Reset));
  Register #(.width(1)) Write_C (.D(or_5_out), .en(Phase2), .clk(Clock), .Q(Write_C_q), .clr(Reset));
  or or_5 (or_5_out, Next_Decoded_Instruction[9], Next_Decoded_Instruction[7], Next_Decoded_Instruction[8], Next_Decoded_Instruction[4], Next_Decoded_Instruction[2], Next_Decoded_Instruction[5]);
  Register #(.width(1)) LUI (.D(Next_Decoded_Instruction[5]), .en(Phase2), .clk(Clock), .Q(LUI_q), .clr(Reset));
  Register #(.width(1)) Branch (.D(Next_Decoded_Instruction[6]), .en(Phase2), .clk(Clock), .Q(Branch_q), .clr(Reset));
  not not_2 (not_2_out, CNZV[2]);
  xor xor_1 (xor_1_out, CNZV[3], CNZV[1]);
  not not_3 (not_3_out, xor_1_out);
  not not_4 (not_4_out, CNZV[0]);
  or or_6 (or_6_out, Next_Decoded_Instruction[7], Next_Decoded_Instruction[8]);
  or or_7 (or_7_out, Next_Decoded_Instruction[6], Next_Decoded_Instruction[8]);
  or or_8 (or_8_out, Load, Store);
  and and_4 (Load_Upper_Immediate, LUI_q, Phase2);
  Multiplexer #(.enable("true"), .select(3)) multiplexer_4 (
    .in0(CNZV[2]), .in1(not_2_out), .in2(1'b0), .in3(1'b0), .in4(xor_1_out), .in5(not_3_out), .in6(CNZV[0]),
    .in7(not_4_out), .out(multiplexer_4_out), .sel(Current_Instruction_Out[14:12]), .en(Branch_q));
  Register #(.width(1)) Unconditional_Jump (
    .D(or_6_out), .en(Phase2), .clk(Clock), .Q(Unconditional_Jump_q), .clr(Reset));
  Register #(.width(1)) PC_Relative_Instruction (.D(or_7_out), .en(Phase2), .clk(Clock), .Q(PC_Relative), .clr(Reset));
  and and_5 (PC_Forward_Address, or_8_out, Phase2);
  and and_6 (and_6_out, Phase1, Last_Load);
  or or_9 (Register_File_Write, and_6_out, and_7_out);
  and and_7 (and_7_out, Phase2, Write_C_q, Not_Exception);
  or or_10 (Jump, multiplexer_4_out, Unconditional_Jump_q);
  and and_8 (PC_Read_Next, Unconditional_Jump_q, Phase2);
  or or_11 (Flush, System_Jump, Jump);
  Multiplexer #(.width(5)) multiplexer_5 (
    .in0(5'b10000), .in1({Next_Funct7[5], Next_Funct7[1], Next_Funct3}), .out(multiplexer_5_out),
    .sel(Next_Decoded_Instruction[4]));
  Register #(.width(1)) AUIPC (.D(Next_Decoded_Instruction[2]), .en(Phase2), .clk(Clock), .Q(ALU_Use_PC), .clr(Reset));
  Register #(.width(1)) Use_Immediate (.D(or_12_out), .en(Phase2), .clk(Clock), .Q(ALU_Use_Immediate), .clr(Reset));
  or or_12 (or_12_out, Next_Decoded_Instruction[2], Next_Decoded_Instruction[1]);
  Register #(.width(5)) OP_Function (.D(multiplexer_5_out), .en(Phase2), .clk(Clock), .Q(ALU_OP_Function), .clr(Reset));
  and and_9 (Input_Buffer_Read, Last_Load, Phase1);
  and and_10 (PAD_Write, Store, Phase2);
  and and_11 (Input_Buffer_Write, Load, Phase2);
  or or_13 (PAD_Data_Size[0], Current_Instruction_Out[12], Current_Instruction_Out[13]);
  or or_14 (PAD_Read, Input_Buffer_Write, Phase1);

  assign PAD_Data_Size[1] = Current_Instruction_Out[13];
  assign Register_Addresses[14:5] = Current_Instruction_Out[24:15];

  // Other names for the same wires on the sheet: Funct3[2:0] = Current_Instruction_Out[14:12];
  //   Next_Immediate = Next_Decoded_Instruction[1]; Next_Add_Upper_Immediate_PC = Next_Decoded_Instruction[2];
  //   Next_Store = Next_Decoded_Instruction[3]; Next_Operation = Next_Decoded_Instruction[4];
  //   Next_Load_Upper_Immediate = Next_Decoded_Instruction[5]; Next_Branch = Next_Decoded_Instruction[6];
  //   Next_Jump_And_Link_Register = Next_Decoded_Instruction[7]; Next_Jump_And_Link = Next_Decoded_Instruction[8];
  //   Next_System = Next_Decoded_Instruction[9]; Phase1n = Phase1; Phase2n = Phase2

  // Notes on the sheet:
  //   Misc
  //   Register File
  //   Program Counter
  //   ALU And Shifter
  //   Input/Output and interface Pads
endmodule

module Immediate_Decoder (
  input  Upper_Immediate,
  input  Jump,
  input  Branch,
  input  Store,
  input  [31:0] Instruction,
  output [31:0] Immediate
);

  wire [1:0] or_2_out;
  wire [11:0] multiplexer_1_out;
  wire [31:0] bit_extender_1_out, bit_extender_2_out, bit_extender_3_out;

  Multiplexer #(.width(12)) multiplexer_1 (
    .in0(Instruction[31:20]), .in1({Instruction[31:25], Instruction[11:7]}), .out(multiplexer_1_out),
    .sel(Store));
  assign bit_extender_1_out = {{19{Instruction[31]}}, {Instruction[31], Instruction[7], Instruction[30:25], Instruction[11:8], 1'b0}};  // Bit_Extender bit_extender_1
  assign bit_extender_2_out = {{11{Instruction[31]}}, {Instruction[31], Instruction[19:12], Instruction[20], Instruction[30:21], 1'b0}};  // Bit_Extender bit_extender_2
  assign bit_extender_3_out = {{20{multiplexer_1_out[11]}}, multiplexer_1_out};  // Bit_Extender bit_extender_3
  or or_1 (or_2_out[1], Upper_Immediate, Jump);
  or or_2 (or_2_out[0], Jump, Branch);
  Multiplexer #(.select(2), .width(32)) multiplexer_2 (
    .in0(bit_extender_3_out), .in1(bit_extender_1_out), .in2({Instruction[31:12], {12{1'b0}}}),
    .in3(bit_extender_2_out), .out(Immediate), .sel(or_2_out));

  // Notes on the sheet:
  //   I-type
  //   S-type
  //   B-type
  //   U-type
  //   J-type
endmodule

module Load_Store_Decoder (
  input  [6:0] OPCODE,
  output LOAD
);

  wire not_1_out, not_2_out, not_3_out, not_4_out;

  not not_1 (not_1_out, OPCODE[6]);
  not not_2 (not_2_out, OPCODE[5]);
  not not_3 (not_3_out, OPCODE[4]);
  not not_4 (not_4_out, OPCODE[3]);
  and and_1 (LOAD, not_1_out, not_2_out, not_3_out, not_4_out, OPCODE[1], OPCODE[0]);
endmodule

module Multiplication (
  input  [31:0] A,
  input  [31:0] B,
  input  [1:0] Sign,
  output [31:0] R_Low,
  output [31:0] R_High
);

  wire [32:31] multiplier_1_cout;
  wire [32:32] and_1_out, and_2_out;

  and and_1 (and_1_out[32], A[31], Sign[0]);
  and and_2 (and_2_out[32], B[31], Sign[1]);
  Multiplier #(.mode("twosComplement"), .width(33)) multiplier_1 (
    .a({and_1_out[32], A}), .b({and_2_out[32], B}), .out({R_High[0], R_Low}),
    .cout({multiplier_1_cout, R_High[31:1]}));  // open: cin
endmodule

module Address_Selector (
  input  Read_In,
  input  [31:0] Address_In,
  input  [31:0] Min_Address,
  input  [31:0] Max_Address,
  input  Write_In,
  output [31:0] Address_Out,
  output Read_Out,
  output Write_Out
);

  wire and_1_out, comparator_1_eq, comparator_1_gt, comparator_2_lt, or_1_out;

  Comparator #(.width(32)) comparator_1 (
    .a(Address_In), .b(Min_Address), .gt(comparator_1_gt), .eq(comparator_1_eq));  // open: lt
  Comparator #(.width(32)) comparator_2 (.a(Address_In), .b(Max_Address), .lt(comparator_2_lt));  // open: gt, eq
  or or_1 (or_1_out, comparator_1_gt, comparator_1_eq);
  and and_1 (and_1_out, or_1_out, comparator_2_lt);
  and and_2 (Read_Out, Read_In, and_1_out);
  and and_3 (Write_Out, and_1_out, Write_In);

  assign Address_Out = Address_In;
endmodule

module CSR_Controller (
  input  Phase1,
  input  Phase2,
  input  [31:0] A_Bus,
  input  [31:0] Next_Instruction,
  input  [31:0] Current_Instruction,
  input  [31:0] Calculated_Address,
  input  Reset,
  input  Clock,
  input  Store,
  input  Load,
  input  Jump,
  input  [31:0] Current_PC,
  input  Pad_Software_Interrupt,
  input  Pad_Timer_Interrupt,
  input  Pad_External_Interrupt,
  input  [9:0] Next_Decoded_Instruction,
  output [31:0] C_Bus,
  output Exception,
  output System_Jump,
  output Next_System_Load,
  output System_Load_Out,
  output [31:0] System_Target_Address,
  output Read_CSR
);

  wire and_1_out, and_3_out, and_4_out, and_5_out, and_6_out, and_7_out, and_8_out, and_9_out, and_10_out,
       and_12_out, and_14_out, and_15_out, and_16_out, and_17_out, and_18_out, and_20_out, and_22_out,
       and_23_out, and_24_out, and_25_out, comparator_1_eq, comparator_2_eq, comparator_3_eq,
       comparator_4_eq, comparator_5_eq, comparator_6_eq, comparator_7_eq, comparator_8_eq, comparator_9_eq,
       comparator_10_eq, comparator_11_eq, comparator_12_eq, comparator_13_eq, comparator_14_eq,
       comparator_15_eq, comparator_16_eq, comparator_17_eq, comparator_18_eq, comparator_19_eq,
       comparator_20_eq, comparator_21_eq, comparator_22_eq, comparator_23_eq, comparator_24_eq,
       decoder_1_out0, decoder_1_out1, decoder_2_out0, decoder_2_out1, decoder_2_out2, decoder_2_out3,
       decoder_3_out0, decoder_3_out1, decoder_3_out2, decoder_3_out3, decoder_4_out0, decoder_4_out1,
       ebreak, ecall, Illegal_Instruction, Interrupt, Interrupt_Enabled, m_cycle_carry, m_inst_ret_carry,
       Misaligned_Address, Misaligned_Data, mret, multiplexer_6_out, multiplexer_7_out, multiplexer_12_out,
       Next_Illegal_CSR, Next_Illegal_System, nor_1_out, nor_2_out, nor_3_out, nor_4_out, or_1_out, or_3_out,
       or_4_out, or_5_out, or_6_out, or_7_out, or_11_out, or_12_out, or_14_out, or_15_out, or_16_out,
       or_18_out, or_19_out, or_20_out, or_23_out, or_24_out, or_25_out, or_26_out, or_27_out,
       priority_encoder_3_gs, Privilege, Trap, Write_mstatus, Write_priv;
  wire [1:0] priority_encoder_1_out, priority_encoder_3_out;
  wire [1:1] Previous_Privilege_q;
  wire [2:0] and_26_out, mie, priority_encoder_2_out;
  wire [4:0] and_2_out, bit_extender_1_out, bit_extender_3_out, m_cause_q, m_isa_q, or_13_out;
  wire [5:0] multiplexer_9_out, multiplexer_22_out, Trap_Cause;
  wire [7:7] Prev_Interrupt_Enabled_q;
  wire [29:0] bit_extender_2_out, multiplexer_8_out;
  wire [31:0] and_21_out, bit_extender_4_out, bit_extender_5_out, m_cycle_h_q, m_cycle_q, m_inst_ret_h_q,
       m_inst_ret_q, m_scratch_q, m_t_val_q, m_t_vec, multiplexer_1_out, multiplexer_2_out,
       multiplexer_4_out, multiplexer_5_out, multiplexer_10_out, multiplexer_11_out, multiplexer_13_out,
       multiplexer_14_out, multiplexer_15_out, multiplexer_16_out, multiplexer_17_out, multiplexer_18_out,
       multiplexer_19_out, multiplexer_21_out, or_21_out, Trap_Value;
  wire [31:2] adder_1_out, m_e_pc;
  wire [31:31] m_cause_interrupt_q;

  Comparator #(.width(12)) comparator_1 (
    .a(Next_Instruction[31:20]), .b(12'h300), .eq(comparator_1_eq));  // open: gt, lt
  Comparator #(.width(12)) comparator_2 (
    .a(Next_Instruction[31:20]), .b(12'h304), .eq(comparator_2_eq));  // open: gt, lt
  Comparator #(.width(12)) comparator_3 (
    .a(Next_Instruction[31:20]), .b(12'h310), .eq(comparator_3_eq));  // open: gt, lt
  Comparator #(.width(12)) comparator_4 (
    .a(Next_Instruction[31:20]), .b(12'h341), .eq(comparator_4_eq));  // open: gt, lt
  Comparator #(.width(12)) comparator_5 (
    .a(Next_Instruction[31:20]), .b(12'h343), .eq(comparator_5_eq));  // open: gt, lt
  Comparator #(.width(12)) comparator_6 (
    .a(Next_Instruction[31:20]), .b(12'hc00), .eq(comparator_6_eq));  // open: gt, lt
  Comparator #(.width(12)) comparator_7 (
    .a(Next_Instruction[31:20]), .b(12'hc02), .eq(comparator_7_eq));  // open: gt, lt
  Comparator #(.width(12)) comparator_8 (
    .a(Next_Instruction[31:20]), .b(12'hc81), .eq(comparator_8_eq));  // open: gt, lt
  Comparator #(.width(12)) comparator_9 (
    .a(Next_Instruction[31:20]), .b(12'hf11), .eq(comparator_9_eq));  // open: gt, lt
  Comparator #(.width(12)) comparator_10 (
    .a(Next_Instruction[31:20]), .b(12'hf13), .eq(comparator_10_eq));  // open: gt, lt
  Comparator #(.width(12)) comparator_11 (
    .a(Next_Instruction[31:20]), .b({12{1'b0}}), .eq(comparator_11_eq));  // open: gt, lt
  Comparator #(.width(12)) comparator_12 (
    .a(Next_Instruction[31:20]), .b(12'h302), .eq(comparator_12_eq));  // open: gt, lt
  nor nor_1 (nor_1_out, Next_Instruction[12], Next_Instruction[13], Next_Instruction[14]);
  Comparator #(.width(12)) comparator_13 (
    .a(Next_Instruction[31:20]), .b(12'h301), .eq(comparator_13_eq));  // open: gt, lt
  Comparator #(.width(12)) comparator_14 (
    .a(Next_Instruction[31:20]), .b(12'h305), .eq(comparator_14_eq));  // open: gt, lt
  Comparator #(.width(12)) comparator_15 (
    .a(Next_Instruction[31:20]), .b(12'h340), .eq(comparator_15_eq));  // open: gt, lt
  Comparator #(.width(12)) comparator_16 (
    .a(Next_Instruction[31:20]), .b(12'h342), .eq(comparator_16_eq));  // open: gt, lt
  Comparator #(.width(12)) comparator_17 (
    .a(Next_Instruction[31:20]), .b(12'h344), .eq(comparator_17_eq));  // open: gt, lt
  Comparator #(.width(12)) comparator_18 (
    .a(Next_Instruction[31:20]), .b(12'hc01), .eq(comparator_18_eq));  // open: gt, lt
  Comparator #(.width(12)) comparator_19 (
    .a(Next_Instruction[31:20]), .b(12'hc80), .eq(comparator_19_eq));  // open: gt, lt
  Comparator #(.width(12)) comparator_20 (
    .a(Next_Instruction[31:20]), .b(12'hc82), .eq(comparator_20_eq));  // open: gt, lt
  Comparator #(.width(12)) comparator_21 (
    .a(Next_Instruction[31:20]), .b(12'hf12), .eq(comparator_21_eq));  // open: gt, lt
  Comparator #(.width(12)) comparator_22 (
    .a(Next_Instruction[31:20]), .b(12'hf14), .eq(comparator_22_eq));  // open: gt, lt
  Comparator #(.width(12)) comparator_23 (
    .a(Current_Instruction[31:20]), .b(12'hc81), .eq(comparator_23_eq));  // open: gt, lt
  Multiplexer #(.width(32)) multiplexer_1 (
    .in0(32'h81000000), .in1(32'h81000004), .out(multiplexer_1_out), .sel(comparator_23_eq));
  or or_1 (or_1_out, Next_Instruction[12], Next_Instruction[13]);
  nor nor_2 (nor_2_out, Next_Instruction[12], Next_Instruction[13], Next_Instruction[14]);
  Comparator #(.width(12)) comparator_24 (
    .a(Next_Instruction[31:20]), .b(12'h1), .eq(comparator_24_eq));  // open: gt, lt
  and and_1 (and_1_out, Next_Decoded_Instruction[9], comparator_12_eq, nor_1_out);
  assign bit_extender_1_out = {{4{m_t_vec[0]}}, m_t_vec[0]};  // Bit_Extender bit_extender_1
  assign and_2_out = bit_extender_1_out & Trap_Cause[4:0];  // AND_Gate and_2, 5 bits wide
  nor nor_3 (nor_3_out, Next_Decoded_Instruction[0], Next_Decoded_Instruction[1], Next_Decoded_Instruction[2], Next_Decoded_Instruction[3], Next_Decoded_Instruction[4], Next_Decoded_Instruction[5], Next_Decoded_Instruction[6], Next_Decoded_Instruction[7], Next_Decoded_Instruction[8], Next_Decoded_Instruction[9]);
  and and_3 (and_3_out, Next_Decoded_Instruction[9], or_1_out);
  and and_4 (and_4_out, Next_Decoded_Instruction[9], comparator_24_eq, nor_1_out);
  and and_5 (and_5_out, Next_Decoded_Instruction[9], comparator_11_eq, nor_1_out);
  Register #(.width(1)) u_MRET (.D(and_1_out), .en(Phase2), .clk(Clock), .Q(mret), .clr(Reset));
  Multiplexer #(.width(32)) multiplexer_2 (
    .in0({m_e_pc, 2'b00}), .in1(multiplexer_1_out), .out(multiplexer_2_out), .sel(System_Load_Out));
  assign bit_extender_2_out = {{25{and_2_out[4]}}, and_2_out};  // Bit_Extender bit_extender_2
  and and_6 (and_6_out, and_3_out, ~Next_Illegal_CSR);  // AND_Gate
  and and_7 (and_7_out, Next_Illegal_CSR, or_1_out);
  and and_8 (and_8_out, Next_Illegal_System, nor_2_out);
  or or_2 (Misaligned_Address, Calculated_Address[0], Calculated_Address[1]);
  or or_3 (or_3_out, Current_Instruction[12], Current_Instruction[13]);
  or or_4 (or_4_out, comparator_18_eq, comparator_8_eq);
  or or_5 (or_5_out, mret, Exception, Interrupt);
  Adder #(.width(30)) adder_1 (.a(m_t_vec[31:2]), .b(bit_extender_2_out), .out(adder_1_out));  // open: cin, cout
  Register #(.width(1)) Write_CSR (.D(and_6_out), .en(Phase2), .clk(Clock), .Q(Read_CSR), .clr(Reset));
  or or_6 (or_6_out, and_7_out, and_8_out);
  and and_9 (and_9_out, Misaligned_Address, Current_Instruction[13]);
  and and_10 (and_10_out, Calculated_Address[0], Calculated_Address[1], or_3_out);
  or or_7 (or_7_out, comparator_11_eq, comparator_24_eq, comparator_12_eq);
  and and_11 (Next_Illegal_System, ~or_7_out, nor_1_out);  // AND_Gate
  Register #(.width(1)) u_EBREAK (.D(and_4_out), .en(Phase2), .clk(Clock), .Q(ebreak), .clr(Reset));
  and and_12 (and_12_out, ~Privilege, Next_Instruction[28]);  // AND_Gate
  nor nor_4 (nor_4_out, comparator_1_eq, comparator_13_eq, comparator_2_eq, comparator_14_eq, comparator_3_eq, comparator_15_eq, comparator_4_eq, comparator_16_eq, comparator_5_eq, comparator_17_eq, comparator_6_eq, comparator_18_eq, comparator_7_eq, comparator_19_eq, comparator_8_eq, comparator_20_eq, comparator_9_eq, comparator_21_eq, comparator_10_eq, comparator_22_eq);
  and and_13 (Next_System_Load, or_4_out, Read_CSR);
  Priority_Encoder #(.select(2)) priority_encoder_1 (
    .in0(1'b0), .in1(mret), .in2(Exception), .in3(Interrupt), .out(priority_encoder_1_out), .en_in(or_5_out));  // open: gs, en_out
  Multiplexer #(.select(2), .width(32)) multiplexer_3 (
    .in0(multiplexer_2_out), .in1({m_e_pc, 2'b00}), .in2({m_t_vec[31:2], 2'b00}), .in3({adder_1_out, 2'b00}),
    .out(System_Target_Address), .sel(priority_encoder_1_out));
  or or_8 (Misaligned_Data, and_9_out, and_10_out);
  or or_9 (Next_Illegal_CSR, and_12_out, nor_4_out);
  Register #(.width(1)) System_Load (.D(Next_System_Load), .en(Phase2), .clk(Clock), .Q(System_Load_Out), .clr(Reset));
  Register #(.width(1)) u_ECALL (.D(and_5_out), .en(Phase2), .clk(Clock), .Q(ecall), .clr(Reset));
  or or_10 (System_Jump, mret, Trap);
  and and_14 (and_14_out, Next_Decoded_Instruction[9], or_6_out);
  or or_11 (or_11_out, nor_3_out, and_14_out);
  Register #(.width(1)) u_Illegal_Instruction (
    .D(or_11_out), .en(Phase2), .clk(Clock), .Q(Illegal_Instruction), .clr(Reset));
  and and_15 (and_15_out, Phase2, ~Illegal_Instruction, Read_CSR);  // AND_Gate
  and and_16 (and_16_out, and_15_out, ~Current_Instruction[30], Current_Instruction[28]);  // AND_Gate
  Decoder decoder_1 (.out0(decoder_1_out0), .out1(decoder_1_out1), .sel(Current_Instruction[26]), .en(and_16_out));
  and and_17 (and_17_out, decoder_1_out1, ~Current_Instruction[22]);  // AND_Gate
  Decoder #(.select(2)) decoder_2 (
    .out0(decoder_2_out0), .out1(decoder_2_out1), .out2(decoder_2_out2), .out3(decoder_2_out3),
    .sel({Current_Instruction[22], Current_Instruction[20]}), .en(decoder_1_out0));
  Decoder #(.select(2)) decoder_3 (
    .out0(decoder_3_out0), .out1(decoder_3_out1), .out2(decoder_3_out2), .out3(decoder_3_out3),
    .sel(Current_Instruction[21:20]), .en(and_17_out));
  assign bit_extender_3_out = {{4{Reset}}, Reset};  // Bit_Extender bit_extender_3
  assign bit_extender_4_out = {{27{1'b0}}, Current_Instruction[24:20]};  // Bit_Extender bit_extender_4
  and and_18 (and_18_out, Privilege, Trap);
  or or_12 (or_12_out, Interrupt_Enabled, ~Trap);  // OR_Gate
  assign or_13_out = bit_extender_3_out | {multiplexer_11_out[30], multiplexer_11_out[20], multiplexer_11_out[12], multiplexer_11_out[8], multiplexer_11_out[4]};  // OR_Gate or_13, 5 bits wide
  or or_14 (or_14_out, decoder_2_out1, Reset);
  Multiplexer #(.width(32)) multiplexer_4 (
    .in0(multiplexer_11_out), .in1(32'h80000001), .out(multiplexer_4_out), .sel(Reset));
  or or_15 (or_15_out, decoder_2_out3, Reset);
  Multiplexer #(.width(32)) multiplexer_5 (
    .in0(A_Bus), .in1(bit_extender_4_out), .out(multiplexer_5_out), .sel(Current_Instruction[14]));
  Multiplexer multiplexer_6 (.in0(and_18_out), .in1(multiplexer_11_out[12]), .out(multiplexer_6_out), .sel(Read_CSR));
  Multiplexer multiplexer_7 (.in0(or_12_out), .in1(multiplexer_11_out[7]), .out(multiplexer_7_out), .sel(Read_CSR));
  or or_16 (or_16_out, Exception, Interrupt);
  Multiplexer #(.width(30)) multiplexer_8 (
    .in0(multiplexer_11_out[31:2]), .in1(Current_PC[31:2]), .out(multiplexer_8_out), .sel(Trap));
  Multiplexer #(.width(6)) multiplexer_9 (
    .in0({multiplexer_11_out[31], multiplexer_11_out[4:0]}), .in1(Trap_Cause), .out(multiplexer_9_out),
    .sel(Trap));
  Multiplexer #(.width(32)) multiplexer_10 (
    .in0(multiplexer_11_out), .in1(Trap_Value), .out(multiplexer_10_out), .sel(Trap));
  Register #(.width(1)) Previous_Privilege (
    .D(multiplexer_6_out), .en(Write_mstatus), .clk(Clock), .Q(Previous_Privilege_q[1]), .clr(Reset));
  Register #(.width(1)) Prev_Interrupt_Enabled (
    .D(multiplexer_7_out), .en(Write_mstatus), .clk(Clock), .Q(Prev_Interrupt_Enabled_q[7]), .clr(Reset));
  and and_19 (Trap, Phase2, or_16_out);
  Register #(.width(30)) u_m_t_vec (
    .D(multiplexer_4_out[31:2]), .en(or_15_out), .clk(Clock), .Q(m_t_vec[31:2]));  // open: clr
  Multiplexer #(.select(2), .width(32)) multiplexer_11 (
    .in0(multiplexer_5_out), .in1(multiplexer_5_out), .in2(or_21_out), .in3(and_21_out),
    .out(multiplexer_11_out), .sel(Current_Instruction[13:12]));
  or or_17 (Write_priv, Trap, mret);
  Register #(.width(5)) m_isa (
    .D({or_13_out[4:1], or_13_out[1]}), .en(or_14_out), .clk(Clock), .Q(m_isa_q));  // open: clr
  Register #(.width(3)) m_i_e (
    .D({multiplexer_11_out[11], multiplexer_11_out[7], multiplexer_11_out[3]}), .en(decoder_2_out2),
    .clk(Clock), .Q(mie), .clr(Reset));
  Register #(.width(1)) m_t_vec_vectored (
    .D(multiplexer_4_out[0]), .en(or_15_out), .clk(Clock), .Q(m_t_vec[0]));  // open: clr
  Register #(.width(32)) m_scratch (
    .D(multiplexer_11_out), .en(decoder_3_out0), .clk(Clock), .Q(m_scratch_q), .clr(Reset));
  Register #(.width(30)) u_m_e_pc (.D(multiplexer_8_out), .en(or_18_out), .clk(Clock), .Q(m_e_pc), .clr(Reset));
  or or_18 (or_18_out, Trap, decoder_3_out1);
  or or_19 (or_19_out, Trap, decoder_3_out2);
  Register #(.width(5)) m_cause (.D(multiplexer_9_out[4:0]), .en(or_19_out), .clk(Clock), .Q(m_cause_q), .clr(Reset));
  Register #(.width(32)) m_t_val (.D(multiplexer_10_out), .en(or_20_out), .clk(Clock), .Q(m_t_val_q), .clr(Reset));
  or or_20 (or_20_out, Trap, decoder_3_out3);
  Counter #(.max('hffffffff), .width(32)) m_cycle (
    .count(1'b1), .Q(m_cycle_q), .carry(m_cycle_carry), .clk(Clock), .clr(Reset));  // open: load, D, up
  and and_20 (and_20_out, Phase2, ~Exception);  // AND_Gate
  Counter #(.max('hffffffff), .width(32)) m_inst_ret (
    .count(and_20_out), .Q(m_inst_ret_q), .carry(m_inst_ret_carry), .clk(Clock), .clr(Reset));  // open: load, D, up
  assign or_21_out = multiplexer_5_out | C_Bus;  // OR_Gate or_21, 32 bits wide
  assign and_21_out = ~multiplexer_5_out & C_Bus;  // AND_Gate and_21, 32 bits wide
  or or_22 (Write_mstatus, decoder_2_out0, Write_priv);
  Register #(.width(1)) m_cause_interrupt (
    .D(multiplexer_9_out[5]), .en(or_19_out), .clk(Clock), .Q(m_cause_interrupt_q[31]), .clr(Reset));
  or or_23 (or_23_out, Previous_Privilege_q[1], Trap, Reset);
  and and_22 (and_22_out, Prev_Interrupt_Enabled_q[7], ~Trap);  // AND_Gate
  Multiplexer multiplexer_12 (.in0(and_22_out), .in1(multiplexer_11_out[3]), .out(multiplexer_12_out), .sel(Read_CSR));
  Counter #(.max('hffffffff), .width(32)) m_cycle_h (
    .count(m_cycle_carry), .Q(m_cycle_h_q), .clk(Clock), .clr(Reset));  // open: load, D, carry, up
  Counter #(.max('hffffffff), .width(32)) m_inst_ret_h (
    .count(m_inst_ret_carry), .Q(m_inst_ret_h_q), .clk(Clock), .clr(Reset));  // open: load, D, carry, up
  Register #(.width(1)) u_Privilege (.D(or_23_out), .en(or_24_out), .clk(Clock), .Q(Privilege));  // open: clr
  or or_24 (or_24_out, Write_priv, Reset);
  Register #(.width(1)) u_Interrupt_Enabled (
    .D(multiplexer_12_out), .en(Write_mstatus), .clk(Clock), .Q(Interrupt_Enabled), .clr(Reset));
  Multiplexer #(.select(2), .width(32)) multiplexer_13 (
    .in0({{19{1'b0}}, {2{Previous_Privilege_q[1]}}, 3'b000, Prev_Interrupt_Enabled_q[7], 3'b000, Interrupt_Enabled, 3'b000}),
    .in1({1'b0, m_isa_q[4], {9{1'b0}}, m_isa_q[3], {7{1'b0}}, m_isa_q[2], 3'b000, m_isa_q[1], 3'b000, m_isa_q[0], 4'b0000}),
    .in2({{20{1'b0}}, mie[2], 3'b000, mie[1], 3'b000, mie[0], 3'b000}),
    .in3({m_t_vec[31:2], 1'b0, m_t_vec[0]}), .out(multiplexer_13_out),
    .sel({Current_Instruction[22], Current_Instruction[20]}));
  Multiplexer #(.select(2), .width(32)) multiplexer_14 (
    .in0(m_scratch_q), .in1({m_e_pc, 2'b00}), .in2({m_cause_interrupt_q[31], {26{1'b0}}, m_cause_q}),
    .in3(m_t_val_q), .out(multiplexer_14_out), .sel(Current_Instruction[21:20]));
  Multiplexer #(.select(2), .width(32)) multiplexer_15 (
    .in0({32{1'b0}}), .in1(32'haf001d), .in2(32'hf0f0f0f0), .in3(32'h4), .out(multiplexer_15_out),
    .sel(Current_Instruction[21:20]));
  Multiplexer #(.width(32)) multiplexer_16 (
    .in0(multiplexer_14_out),
    .in1({{20{1'b0}}, Pad_External_Interrupt, 3'b000, Pad_Timer_Interrupt, 3'b000, Pad_Software_Interrupt, 3'b000}),
    .out(multiplexer_16_out), .sel(Current_Instruction[22]));
  Multiplexer #(.select(2), .width(32)) multiplexer_17 (
    .in0(m_cycle_q), .in1(m_inst_ret_q), .in2(m_cycle_h_q), .in3(m_inst_ret_h_q), .out(multiplexer_17_out),
    .sel({Current_Instruction[27], Current_Instruction[21]}));
  Multiplexer #(.width(32)) multiplexer_18 (
    .in0(multiplexer_13_out), .in1(multiplexer_16_out), .out(multiplexer_18_out),
    .sel(Current_Instruction[26]));
  Multiplexer #(.width(32)) multiplexer_19 (
    .in0(multiplexer_17_out), .in1(multiplexer_15_out), .out(multiplexer_19_out),
    .sel(Current_Instruction[28]));
  Multiplexer #(.width(32)) multiplexer_20 (
    .in0(multiplexer_18_out), .in1(multiplexer_19_out), .out(C_Bus), .sel(Current_Instruction[30]));
  Decoder decoder_4 (.out0(decoder_4_out0), .out1(decoder_4_out1), .sel(Privilege), .en(ecall));
  and and_23 (and_23_out, Misaligned_Data, Store);
  and and_24 (and_24_out, Misaligned_Data, Load, ~System_Load_Out);  // AND_Gate
  and and_25 (and_25_out, Misaligned_Address, Jump);
  or or_25 (or_25_out, and_23_out, and_24_out, decoder_4_out0, decoder_4_out1, ebreak, and_25_out, Illegal_Instruction);
  Priority_Encoder priority_encoder_2 (
    .in0(1'b0), .in1(and_23_out), .in2(and_24_out), .in3(decoder_4_out0), .in4(decoder_4_out1), .in5(ebreak),
    .in6(and_25_out), .in7(Illegal_Instruction), .out(priority_encoder_2_out), .en_in(or_25_out),
    .gs(Exception));  // open: en_out
  Multiplexer #(.select(3), .width(32)) multiplexer_21 (
    .in0({32{1'b0}}), .in1(Calculated_Address), .in2(Calculated_Address), .in3({32{1'b0}}), .in4({32{1'b0}}),
    .in5({32{1'b0}}), .in6(Calculated_Address), .in7(Current_Instruction), .out(multiplexer_21_out),
    .sel(priority_encoder_2_out));
  Multiplexer #(.select(3), .width(6)) multiplexer_22 (
    .in0({6{1'b0}}), .in1(6'b000110), .in2(6'b000100), .in3(6'b001000), .in4(6'b001011), .in5(6'b000011),
    .in6({6{1'b0}}), .in7(6'b000010), .out(multiplexer_22_out), .sel(priority_encoder_2_out));
  assign and_26_out = {Pad_External_Interrupt, Pad_Timer_Interrupt, Pad_Software_Interrupt} & mie;  // AND_Gate and_26, 3 bits wide
  or or_26 (or_26_out, and_26_out[2], and_26_out[1], and_26_out[0]);
  or or_27 (or_27_out, Interrupt_Enabled, ~Privilege);  // OR_Gate
  Priority_Encoder #(.select(2)) priority_encoder_3 (
    .in0(1'b0), .in1(and_26_out[2]), .in2(and_26_out[1]), .in3(and_26_out[0]), .out(priority_encoder_3_out),
    .gs(priority_encoder_3_gs), .en_in(or_26_out));  // open: en_out
  and and_27 (Interrupt, or_27_out, priority_encoder_3_gs);
  Multiplexer #(.select(2), .width(6)) multiplexer_23 (
    .in0(multiplexer_22_out), .in1(6'b101011), .in2(6'b100111), .in3(6'b100011), .out(Trap_Cause),
    .sel(priority_encoder_3_out));
  assign Trap_Value = multiplexer_21_out & ~bit_extender_5_out;  // AND_Gate and_28, 32 bits wide
  assign bit_extender_5_out = {{31{Interrupt}}, Interrupt};  // Bit_Extender bit_extender_5

  // Other names for the same wires on the sheet: mip[2:0] = {Pad_External_Interrupt, Pad_Timer_Interrupt, Pad_Software_Interrupt};
  //   Funct_3[2:0] = Current_Instruction[14:12]; Funct_12[11:0] = Current_Instruction[31:20];
  //   Immediate_5bit[4:0] = Current_Instruction[24:20]; Next_System = Next_Decoded_Instruction[9];
  //   Next_Funct_3[2:0] = Next_Instruction[14:12]; Next_Funct_12[11:0] = Next_Instruction[31:20];
  //   System_Load = System_Load_Out; Write_CSR = Read_CSR

  // Notes on the sheet:
  //   m_hart_id
  //   m_vendor_id
  //   m_arch_id
  //   m_imp_id
  //   m_status
  //   m_i_p
  //   Interrupt and Exception Controls
endmodule

module Register_History_Generator (
  input  [31:0] Current_Value,
  input  [4:0] Current_Address,
  input  [4:0] Target_Address,
  input  Write_Signal,
  input  Reset,
  input  Clock,
  output Out_Clock,
  output [15:0] Out_Value
);

  wire and_1_out, comparator_1_eq, comparator_2_gt;
  wire [3:0] counter_1_q;
  wire [31:0] Last_Value_q, register_1_q;

  Comparator #(.width(5)) comparator_1 (.a(Current_Address), .b(Target_Address), .eq(comparator_1_eq));  // open: gt, lt
  and and_1 (and_1_out, comparator_1_eq, Write_Signal);
  Register #(.trigger("falling"), .width(32)) register_1 (
    .D(Current_Value), .en(and_1_out), .clk(Clock), .Q(register_1_q));  // open: clr
  Register #(.trigger("falling"), .width(32)) Last_Value (
    .D(Current_Value), .en(and_1_out), .clk(Clock), .Q(Last_Value_q), .clr(Reset));
  and and_2 (Out_Clock, and_1_out, Clock);
  Comparator #(.width(32)) comparator_2 (.a(register_1_q), .b(Last_Value_q), .gt(comparator_2_gt));  // open: eq, lt
  Counter #(.max('hf), .width(4)) counter_1 (
    .clr(Reset), .up(comparator_2_gt), .count(and_1_out), .clk(Clock), .Q(counter_1_q));  // open: load, D, carry
  Decoder #(.enable("false"), .select(4)) decoder_1 (
    .out0(Out_Value[0]), .out1(Out_Value[1]), .out2(Out_Value[2]), .out3(Out_Value[3]), .out4(Out_Value[4]),
    .out5(Out_Value[5]), .out6(Out_Value[6]), .out7(Out_Value[7]), .out8(Out_Value[8]), .out9(Out_Value[9]),
    .out10(Out_Value[10]), .out11(Out_Value[11]), .out12(Out_Value[12]), .out13(Out_Value[13]),
    .out14(Out_Value[14]), .out15(Out_Value[15]), .sel(counter_1_q));
endmodule

module Real_Time_Device (
  input  [31:0] Data_In,
  input  Clock,
  input  Reset,
  input  Write,
  input  [1:0] Address,
  output Timer_Interrupt,
  output [31:0] Data_Out
);

  wire and_1_out, buffer_1_out, buffer_2_out, decoder_1_out0, decoder_1_out1, decoder_1_out2, decoder_1_out3,
       m_time_carry, not_1_out, or_1_out;
  wire [63:0] m_cmp_time_q, m_time_q;

  Decoder #(.select(2)) decoder_1 (
    .out0(decoder_1_out0), .out1(decoder_1_out1), .out2(decoder_1_out2), .out3(decoder_1_out3),
    .sel(Address), .en(Write));
  buf buffer_1 (buffer_1_out, Clock);
  buf buffer_2 (buffer_2_out, buffer_1_out);
  and and_1 (and_1_out, buffer_2_out, not_1_out);
  not not_1 (not_1_out, Clock);
  or or_1 (or_1_out, and_1_out, Clock);
  Register #(.width(32)) m_cmp_time (
    .D(Data_In), .en(decoder_1_out2), .clk(Clock), .Q(m_cmp_time_q[31:0]), .clr(Reset));
  Counter #(.max('hffffffff), .width(32)) m_time (
    .load(decoder_1_out0), .D(Data_In), .count(1'b1), .Q(m_time_q[31:0]), .carry(m_time_carry),
    .clk(or_1_out), .clr(Reset));  // open: up
  Register #(.width(32)) m_cmp_time_h (
    .D(Data_In), .en(decoder_1_out3), .clk(Clock), .Q(m_cmp_time_q[63:32]), .clr(Reset));
  Counter #(.max('hffffffff), .width(32)) m_time_h (
    .load(decoder_1_out1), .D(Data_In), .count(m_time_carry), .Q(m_time_q[63:32]), .clk(or_1_out), .clr(Reset));  // open: carry, up
  Multiplexer #(.select(2), .width(32)) multiplexer_1 (
    .in0(m_time_q[31:0]), .in1(m_time_q[63:32]), .in2(m_cmp_time_q[31:0]), .in3(m_cmp_time_q[63:32]),
    .out(Data_Out), .sel(Address));
  Comparator #(.mode("unsigned"), .width(64)) comparator_1 (
    .a(m_time_q), .b(m_cmp_time_q), .gt(Timer_Interrupt));  // open: eq, lt
endmodule

module Adder_Subtractor (
  input  Subraction,
  input  [31:0] A,
  input  [31:0] B,
  output [31:0] R,
  output C_Out
);

  wire adder_1_cout;
  wire [31:0] bit_extender_1_out, xor_1_out;

  assign bit_extender_1_out = {{31{Subraction}}, Subraction};  // Bit_Extender bit_extender_1
  assign xor_1_out = bit_extender_1_out ^ B;  // XOR_Gate xor_1, 32 bits wide
  Adder #(.width(32)) adder_1 (.a(A), .b(xor_1_out), .out(R), .cin(Subraction), .cout(adder_1_cout));
  xor xor_2 (C_Out, Subraction, adder_1_cout);
endmodule

module op_debugger (
  input  ph2,
  input  c,
  input  r,
  input  [9:0] DataIn
);

  Register #(.width(1)) register_1 (.D(DataIn[0]), .en(ph2), .clk(c), .clr(r));  // open: Q
  Register #(.width(1)) register_2 (.D(DataIn[1]), .en(ph2), .clk(c), .clr(r));  // open: Q
  Register #(.width(1)) register_3 (.D(DataIn[2]), .en(ph2), .clk(c), .clr(r));  // open: Q
  Register #(.width(1)) register_4 (.D(DataIn[3]), .en(ph2), .clk(c), .clr(r));  // open: Q
  Register #(.width(1)) register_5 (.D(DataIn[4]), .en(ph2), .clk(c), .clr(r));  // open: Q
  Register #(.width(1)) register_6 (.D(DataIn[5]), .en(ph2), .clk(c), .clr(r));  // open: Q
  Register #(.width(1)) register_7 (.D(DataIn[6]), .en(ph2), .clk(c), .clr(r));  // open: Q
  Register #(.width(1)) register_8 (.D(DataIn[7]), .en(ph2), .clk(c), .clr(r));  // open: Q
  Register #(.width(1)) register_9 (.D(DataIn[8]), .en(ph2), .clk(c), .clr(r));  // open: Q
  Register #(.width(1)) register_10 (.D(DataIn[9]), .en(ph2), .clk(c), .clr(r));  // open: Q
endmodule
